// Logisim project 4 bit cpu 23-04-2017.circ as structural Verilog: 1 circuit, main circuit main
module main (
  input  in_1,
  input  [3:0] in_2,
  input  [3:0] in_3,
  input  [3:0] in_4,
  input  [3:0] in_5,
  input  Fetch,
  input  Execute,
  input  [7:0] in_8,
  input  [7:0] in_9,
  output [3:0] out_10,
  output [3:0] out_11,
  output [7:0] To_IR,
  output [3:0] out_13,
  output [3:0] out_14,
  output [3:0] out_15,
  output out_16,
  output [7:0] out_17,
  output out_18,
  output out_19,
  output out_20,
  output out_21,
  output out_22,
  output [1:0] out_23,
  output [1:0] out_24,
  output [1:0] out_25,
  output [1:0] out_26,
  output [5:0] out_27
);

  wire button_1_out, button_2_out, button_3_out, button_4_out, clock_1_out;
  wire [3:0] PC_q;
  wire [5:0] bit_extender_4_out;
  wire [7:0] and_2_out, IR_q;

  Button button_1 (.out(button_1_out));
  LED led_1 (.in(in_1));
  LED led_2 (.in(button_1_out));
  Clock clock_1 (.out(clock_1_out));
  LED Led1 (.in(clock_1_out));
  Controlled_Buffer controlled_buffer_1 (.in(clock_1_out));  // open: out, en
  assign out_13 = button_2_out ? in_4 : 4'bz;  // Controlled_Buffer controlled_buffer_2
  Button button_2 (.out(button_2_out));
  Adder #(.width(4)) adder_1 (.a(in_2), .b(in_3), .out(out_10));  // open: cin, cout
  Hex_Digit_Display hex_digit_display_1 (.value(out_10), .dp(button_3_out));
  Button button_3 (.out(button_3_out));
  Button button_4 (.out(button_4_out));
  Register #(.width(4)) PC (.D(in_5), .Q(PC_q), .clk(button_4_out));  // open: en, clr
  Bit_Extender #(.out_width(6)) bit_extender_1 (.in(in_9), .out(out_27));
  assign out_15 = {{3{Fetch}}, Fetch};  // Bit_Extender bit_extender_2
  assign out_14 = PC_q & out_15;  // AND_Gate and_1, 4 bits wide
  assign out_11 = Fetch ? out_14 : 4'bz;  // Controlled_Buffer controlled_buffer_3
  RAM #(.addrWidth(4), .bus("asynch")) ram_1 (.addr(out_11), .data(To_IR), .sel(Fetch), .ld(1'b1), .clr(1'b0));
  Register IR (.D(To_IR), .Q(IR_q));  // open: en, clk, clr
  assign out_17 = {{7{Execute}}, Execute};  // Bit_Extender bit_extender_3
  assign and_2_out = out_17 & IR_q;  // AND_Gate and_2, 8 bits wide
  Bit_Extender #(.out_width(6)) bit_extender_4 (.in(and_2_out), .out(bit_extender_4_out));

  assign out_16 = in_8[0];
  assign out_18 = in_8[1];
  assign out_19 = in_8[2];
  assign out_20 = in_8[3];
  assign out_21 = in_8[4];
  assign out_22 = in_8[5];
  assign out_23 = in_9[1:0];
  assign out_24 = in_9[3:2];
  assign out_25 = in_9[5:4];
  assign out_26 = in_9[7:6];
endmodule
