// Logisim project 4 bit cpu a - Cópia.circ as structural Verilog: 1 circuit, main circuit main
module main (
  input  in_1,
  input  [3:0] in_2,
  input  [3:0] in_3,
  input  [3:0] in_4,
  input  [3:0] in_5,
  input  Fetch,
  input  Execute,
  input  [7:0] in_8,
  output [3:0] out_9,
  output [3:0] out_10,
  output [7:0] To_IR,
  output [3:0] out_12,
  output [3:0] out_13,
  output [3:0] out_14,
  output out_15,
  output [7:0] out_16,
  output out_17,
  output out_18,
  output [7:0] out_19,
  output out_20,
  output out_21,
  output [5:0] out_22,
  output out_23,
  output [3:0] out_24,
  output [1:0] out_25,
  output [1:0] out_26,
  output [1:0] out_27,
  output [1:0] out_28,
  output [5:0] out_29
);

  wire button_1_out, button_2_out, button_3_out, button_4_out, clock_1_out, decoder_1_out0, decoder_1_out1,
       Instruction_Decoder_p1, Instruction_Decoder_p2;
  wire [3:0] and_3_out, and_4_out, and_5_out, bit_extender_3_out, bit_extender_4_out, bit_extender_5_out,
       PC_q;
  wire [7:0] IR_q;

  Button button_1 (.out(button_1_out));
  LED led_1 (.in(in_1));
  LED led_2 (.in(button_1_out));
  Clock clock_1 (.out(clock_1_out));
  LED Led1 (.in(clock_1_out));
  Controlled_Buffer controlled_buffer_1 (.in(clock_1_out));  // open: out, en
  assign out_12 = button_2_out ? in_4 : 4'bz;  // Controlled_Buffer controlled_buffer_2
  Button button_2 (.out(button_2_out));
  Adder #(.width(4)) adder_1 (.a(in_2), .b(in_3), .out(out_9));  // open: cin, cout
  Hex_Digit_Display hex_digit_display_1 (.value(out_9), .dp(button_3_out));
  Button button_3 (.out(button_3_out));
  Button button_4 (.out(button_4_out));
  Register #(.width(4), .trigger("falling")) PC (.D(in_5), .Q(PC_q), .clk(button_4_out));  // open: en, clr
  assign out_14 = {{3{Fetch}}, Fetch};  // Bit_Extender bit_extender_1
  assign out_13 = PC_q & out_14;  // AND_Gate and_1, 4 bits wide
  assign out_10 = Fetch ? out_13 : 4'bz;  // Controlled_Buffer controlled_buffer_3
  RAM #(.addrWidth(4), .bus("asynch")) ram_1 (.addr(out_10), .data(To_IR), .sel(Fetch), .ld(1'b1), .clr(1'b0));
  // intruction_decoder_2_main Instruction_Decoder: pin names not known; wires that end beside it: Instruction_Decoder_p1, Instruction_Decoder_p2, out_19[7:2]
  Register #(.trigger("falling")) IR (.D(To_IR), .Q(IR_q), .clk(Fetch), .clr(1'b0));  // open: en
  assign out_16 = {{7{Execute}}, Execute};  // Bit_Extender bit_extender_2
  assign out_19 = out_16 & IR_q;  // AND_Gate and_2, 8 bits wide
  Decoder #(.select(2)) decoder_1 (
    .out0(decoder_1_out0), .out1(decoder_1_out1), .sel(out_19[5:4]), .en(1'b1));  // open: out2, out3
  assign bit_extender_3_out = {{3{Instruction_Decoder_p2}}, Instruction_Decoder_p2};  // Bit_Extender bit_extender_3
  assign bit_extender_4_out = {{3{decoder_1_out0}}, decoder_1_out0};  // Bit_Extender bit_extender_4
  assign bit_extender_5_out = {{3{decoder_1_out1}}, decoder_1_out1};  // Bit_Extender bit_extender_5
  assign and_3_out = bit_extender_3_out & out_19[3:0];  // AND_Gate and_3, 4 bits wide
  assign and_4_out = bit_extender_4_out & and_3_out;  // AND_Gate and_4, 4 bits wide
  assign and_5_out = bit_extender_5_out & and_3_out;  // AND_Gate and_5, 4 bits wide
  Register #(.width(4), .trigger("falling")) Register_A (
    .D(and_4_out), .clk(Instruction_Decoder_p2));  // open: en, Q, clr
  Register #(.width(4), .trigger("falling")) Register_B (
    .D(and_5_out), .clk(Instruction_Decoder_p2));  // open: en, Q, clr

  assign out_15 = in_8[0];
  assign out_17 = in_8[1];
  assign out_18 = in_8[2];
  assign out_20 = in_8[3];
  assign out_21 = in_8[4];
  assign out_22 = out_19[7:2];
  assign out_23 = in_8[5];
  assign out_24 = out_19[3:0];
  assign out_29 = {out_25, out_26, out_27};

  // Notes on the sheet:
  //   LD R1, data
  //   Register selection for direct instructions
  //   Data for direct instructions
endmodule
