// Logisim project 4 bit cpu a - before clock change.circ as structural Verilog: 1 circuit, main circuit main
module main (
  input  in_1,
  input  [3:0] in_2,
  input  [3:0] in_3,
  input  [3:0] in_4,
  input  [7:0] in_5,
  output [3:0] out_6,
  output [3:0] out_7,
  output [7:0] To_IR,
  output [3:0] out_9,
  output [3:0] out_10,
  output [3:0] out_11,
  output [7:0] out_12,
  output [7:0] out_13,
  output [5:0] out_14,
  output CLK_A,
  output [3:0] out_16,
  output CLK_B,
  output [3:0] out_18,
  output out_19,
  output out_20,
  output out_21,
  output out_22,
  output [1:0] out_23,
  output [1:0] out_24,
  output [1:0] out_25,
  output [1:0] out_26,
  output out_27,
  output [5:0] out_28,
  output out_29
);

  wire and_4_out, and_5_out, and_6_out, button_1_out, button_2_out, button_3_out, clock_1_out, clock_2_out,
       clock_3_out, decoder_1_out2, decoder_2_out0, decoder_2_out1, decoder_2_out2, decoder_2_out3,
       decoder_3_out0, decoder_3_out1, decoder_3_out2, decoder_3_out3, Instruction_Decoder_add_r1__data,
       Instruction_Decoder_jp, Instruction_Decoder_ld_r1__data, or_1_out, or_3_out, or_4_out, Reset;
  wire [1:0] counter_1_q, counter_2_q;
  wire [3:0] adder_2_out, and_3_out, bit_extender_3_out, controlled_buffer_3_out, controlled_buffer_7_out,
       controlled_buffer_8_out, controlled_buffer_9_out, controlled_buffer_12_out, PC_q, Register_A_q,
       Register_B_q, undriven, undriven_2;
  wire [7:0] IR_q;

  Button button_1 (.out(button_1_out));
  assign out_9 = button_2_out ? in_4 : 4'bz;  // Controlled_Buffer controlled_buffer_1
  Button button_2 (.out(button_2_out));
  Clock clock_1 (.out(clock_1_out));
  LED led_1 (.in(in_1));
  LED led_2 (.in(button_1_out));
  Clock clock_2 (.out(clock_2_out));
  Clock clock_3 (.out(clock_3_out));
  Counter #(.width(2), .max('h3)) counter_1 (
    .load(1'b0), .count(1'b1), .Q(counter_1_q), .clk(clock_1_out));  // open: D, carry, clr
  LED Led1 (.in(clock_2_out));
  Controlled_Buffer controlled_buffer_2 ();  // open: in, out, en
  Counter #(.width(2), .max('h3)) counter_2 (
    .Q(counter_2_q), .clk(clock_3_out), .clr(or_1_out));  // open: load, D, count, carry
  or or_1 (or_1_out, decoder_2_out3, Reset);
  Decoder #(.select(2)) decoder_1 (
    .out2(decoder_1_out2), .out3(CLK_B), .sel(counter_1_q), .en(1'b1));  // open: out0, out1
  Decoder #(.select(2)) decoder_2 (
    .out0(decoder_2_out0), .out1(decoder_2_out1), .out2(decoder_2_out2), .out3(decoder_2_out3),
    .sel(counter_2_q));  // open: en
  LED led_3 (.in(Reset));
  Button u_Reset (.out(Reset));
  Adder #(.width(4)) adder_1 (.a(in_2), .b(in_3), .out(out_6));  // open: cin, cout
  Adder #(.width(4)) adder_2 (.a(PC_q), .b(4'b0001), .out(adder_2_out), .cin(1'b0));  // open: cout
  or or_2 (CLK_A, decoder_1_out2, CLK_B);
  assign controlled_buffer_3_out = decoder_2_out0 ? adder_2_out : 4'bz;  // Controlled_Buffer controlled_buffer_3
  Hex_Digit_Display hex_digit_display_1 (.value(out_6), .dp(button_3_out));
  Button button_3 (.out(button_3_out));
  assign controlled_buffer_3_out = Instruction_Decoder_jp ? out_13[3:0] : 4'bz;  // Controlled_Buffer controlled_buffer_4
  or or_3 (or_3_out, decoder_2_out1, decoder_2_out2);
  Register #(.width(4), .trigger("falling")) PC (
    .D(controlled_buffer_3_out), .en(1'b1), .Q(PC_q), .clk(decoder_2_out0), .clr(Reset));
  assign out_11 = {{3{decoder_2_out0}}, decoder_2_out0};  // Bit_Extender bit_extender_1
  assign out_10 = PC_q & out_11;  // AND_Gate and_1, 4 bits wide
  assign out_7 = decoder_2_out0 ? out_10 : 4'bz;  // Controlled_Buffer controlled_buffer_5
  RAM #(.addrWidth(4), .bus("asynch")) ram_1 (.addr(out_7), .data(To_IR), .sel(decoder_2_out0), .ld(1'b1), .clr(1'b0));
  intruction_decoder_2_main Instruction_Decoder (
    .Chip_Enable(or_3_out), .Input(out_14), .LD_R1__data(Instruction_Decoder_ld_r1__data),
    .ADD_R1__data(Instruction_Decoder_add_r1__data), .JP(Instruction_Decoder_jp));  // open: LD_R1__R2, ADD_R1__R2, SUB_R1__R2, SUB_R1__data, JP_Z
  assign out_14 = or_3_out ? out_13[7:2] : 6'bz;  // Controlled_Buffer controlled_buffer_6
  Register #(.trigger("falling")) IR (.D(To_IR), .Q(IR_q), .clk(decoder_2_out0), .clr(Reset));  // open: en
  assign out_12 = {{7{or_3_out}}, or_3_out};  // Bit_Extender bit_extender_2
  assign out_13 = out_12 & IR_q;  // AND_Gate and_2, 8 bits wide
  Decoder #(.select(2)) decoder_3 (
    .out0(decoder_3_out0), .out1(decoder_3_out1), .out2(decoder_3_out2), .out3(decoder_3_out3),
    .sel(out_13[5:4]), .en(1'b1));
  assign bit_extender_3_out = {{3{Instruction_Decoder_ld_r1__data}}, Instruction_Decoder_ld_r1__data};  // Bit_Extender bit_extender_3
  assign and_3_out = bit_extender_3_out & out_13[3:0];  // AND_Gate and_3, 4 bits wide
  and and_4 (and_4_out, decoder_3_out0, Instruction_Decoder_ld_r1__data);
  and and_5 (and_5_out, decoder_3_out1, Instruction_Decoder_ld_r1__data);
  or or_4 (or_4_out, Instruction_Decoder_add_r1__data, Instruction_Decoder_ld_r1__data);
  and and_6 (and_6_out, or_4_out, decoder_2_out2);
  assign controlled_buffer_7_out = Instruction_Decoder_add_r1__data ? out_18 : 4'bz;  // Controlled_Buffer controlled_buffer_7
  assign controlled_buffer_8_out = and_4_out ? and_3_out : 4'bz;  // Controlled_Buffer controlled_buffer_8
  assign controlled_buffer_9_out = and_5_out ? and_3_out : 4'bz;  // Controlled_Buffer controlled_buffer_9
  assign controlled_buffer_8_out = decoder_3_out0 ? controlled_buffer_7_out : 4'bz;  // Controlled_Buffer controlled_buffer_10
  assign controlled_buffer_9_out = decoder_3_out1 ? controlled_buffer_7_out : 4'bz;  // Controlled_Buffer controlled_buffer_11
  Register #(.width(4), .trigger("falling")) Register_A (
    .D(controlled_buffer_8_out), .en(1'b1), .Q(Register_A_q), .clk(and_6_out), .clr(Reset));
  assign controlled_buffer_12_out = decoder_3_out0 ? Register_A_q : 4'bz;  // Controlled_Buffer controlled_buffer_12
  Register #(.width(4), .trigger("falling")) Register_B (
    .D(controlled_buffer_9_out), .en(1'b1), .Q(Register_B_q), .clk(and_6_out), .clr(Reset));
  assign controlled_buffer_12_out = decoder_3_out1 ? Register_B_q : 4'bz;  // Controlled_Buffer controlled_buffer_13
  Register #(.width(4), .trigger("falling")) Register_C (.D(undriven), .clk(and_6_out), .clr(Reset));  // open: en, Q
  Register #(.width(4), .trigger("falling")) Register_D (.D(undriven_2), .clk(and_6_out), .clr(Reset));  // open: en, Q
  Adder #(.width(4)) adder_3 (.a(controlled_buffer_12_out), .b(out_13[3:0]), .out(out_18), .cin(1'b0));  // open: cout
  Adder #(.width(4)) adder_4 ();  // open: a, b, out, cin, cout

  assign out_16 = out_13[3:0];
  assign out_19 = in_5[0];
  assign out_20 = in_5[1];
  assign out_21 = in_5[2];
  assign out_22 = in_5[3];
  assign out_27 = in_5[4];
  assign out_28 = {out_23, out_24, out_25};
  assign out_29 = in_5[5];

  // Notes on the sheet:
  //   Fetch
  //   Decode
  //   Execute
  //   JP addr
  //   ADD R1, data
  //   LD R1, data
  //   Register selection for imediate instructions
  //   Data for imediate instructions
  //   or address for direct instructions
endmodule
