// Logisim project 4 bit cpu a 17-05-2017.circ as structural Verilog: 1 circuit, main circuit main
module main (
  input  in_1,
  input  [3:0] in_2,
  input  [3:0] in_3,
  input  [3:0] in_4,
  input  [7:0] in_5,
  output [3:0] out_6,
  output [3:0] out_7,
  output [7:0] To_IR,
  output [3:0] out_9,
  output [3:0] out_10,
  output CLK_A,
  output [3:0] out_12,
  output [7:0] out_13,
  output [7:0] out_14,
  output [5:0] out_15,
  output CLK_B,
  output [3:0] out_17,
  output [3:0] out_18,
  output [3:0] out_19,
  output out_20,
  output out_21,
  output out_22,
  output out_23,
  output [1:0] out_24,
  output [1:0] out_25,
  output [1:0] out_26,
  output [1:0] out_27,
  output out_28,
  output [5:0] out_29,
  output out_30,
  output out_31
);

  wire and_1_out, and_2_out, and_6_out, and_7_out, and_8_out, and_9_out, and_10_out, and_11_out,
       button_1_out, button_2_out, button_3_out, clock_1_out, clock_2_out, decoder_1_out0, decoder_2_out0,
       decoder_2_out1, decoder_2_out2, decoder_3_out0, decoder_3_out1, decoder_3_out2, decoder_3_out3,
       decoder_4_out0, decoder_4_out1, decoder_5_out0, decoder_5_out1, Instruction_Decoder_add_r1__data,
       Instruction_Decoder_add_r1__r2, Instruction_Decoder_jp, Instruction_Decoder_ld_r1__data,
       Instruction_Decoder_ld_r1__r2, Instruction_Decoder_sub_r1__data, or_2_out, or_3_out, or_4_out,
       or_5_out, or_6_out, Reset, undriven;
  wire [1:0] counter_1_q, counter_2_q;
  wire [3:0] adder_2_out, and_5_out, bit_extender_3_out, controlled_buffer_3_out, controlled_buffer_8_out,
       controlled_buffer_9_out, controlled_buffer_10_out, controlled_buffer_13_out, controlled_buffer_14_out,
       controlled_buffer_20_out, controlled_buffer_24_out, controlled_buffer_26_out, PC_q, Register_A_q,
       Register_B_q, Register_C_q, Register_D_q, undriven_2;
  wire [7:0] IR_q;

  Button button_1 (.out(button_1_out));
  assign out_9 = button_2_out ? in_4 : 4'bz;  // Controlled_Buffer controlled_buffer_1
  Button button_2 (.out(button_2_out));
  Decoder #(.select(2)) decoder_1 (
    .out0(decoder_1_out0), .out1(CLK_B), .sel(counter_1_q), .en(1'b1));  // open: out2, out3
  Counter #(.width(2), .max('h3)) counter_1 (
    .load(1'b0), .count(1'b1), .Q(counter_1_q), .clk(clock_1_out), .clr(Reset));  // open: D, carry
  Clock clock_1 (.out(clock_1_out));
  LED led_1 (.in(in_1));
  LED led_2 (.in(button_1_out));
  Clock clock_2 (.out(clock_2_out));
  or or_1 (CLK_A, decoder_1_out0, CLK_B);
  LED Led1 (.in(clock_2_out));
  Controlled_Buffer controlled_buffer_2 ();  // open: in, out, en
  Counter #(.width(2), .max('h3)) counter_2 (
    .Q(counter_2_q), .clk(CLK_A), .clr(or_2_out));  // open: load, D, count, carry
  or or_2 (or_2_out, decoder_2_out2, Reset);
  Decoder #(.select(2)) decoder_2 (
    .out0(decoder_2_out0), .out1(decoder_2_out1), .out2(decoder_2_out2), .sel(counter_2_q));  // open: out3, en
  LED led_3 (.in(Reset));
  Button u_Reset (.out(Reset));
  Adder #(.width(4)) adder_1 (.a(in_2), .b(in_3), .out(out_6));  // open: cin, cout
  Adder #(.width(4)) adder_2 (.a(PC_q), .b(4'b0001), .out(adder_2_out), .cin(1'b0));  // open: cout
  and and_1 (and_1_out, decoder_2_out0, CLK_B);
  assign controlled_buffer_3_out = decoder_2_out0 ? adder_2_out : 4'bz;  // Controlled_Buffer controlled_buffer_3
  Hex_Digit_Display hex_digit_display_1 (.value(out_6), .dp(button_3_out));
  Button button_3 (.out(button_3_out));
  or or_3 (or_3_out, and_1_out, and_2_out);
  assign controlled_buffer_3_out = Instruction_Decoder_jp ? out_14[3:0] : 4'bz;  // Controlled_Buffer controlled_buffer_4
  Register #(.width(4)) PC (.D(controlled_buffer_3_out), .en(1'b1), .Q(PC_q), .clk(or_3_out), .clr(Reset));
  and and_2 (and_2_out, CLK_B, Instruction_Decoder_jp);
  assign out_12 = {{3{decoder_2_out0}}, decoder_2_out0};  // Bit_Extender bit_extender_1
  assign out_10 = PC_q & out_12;  // AND_Gate and_3, 4 bits wide
  assign out_7 = decoder_2_out0 ? out_10 : 4'bz;  // Controlled_Buffer controlled_buffer_5
  assign out_31 = undriven ? 1'b1 : 1'bz;  // Controlled_Buffer controlled_buffer_6
  Button button_4 ();  // open: out
  RAM #(.addrWidth(4), .bus("asynch")) ram_1 (.addr(out_7), .data(To_IR), .sel(decoder_2_out0), .ld(1'b1), .clr(1'b0));
  intruction_decoder_2_main Instruction_Decoder (
    .Chip_Enable(decoder_2_out1), .Input(out_15), .LD_R1__R2(Instruction_Decoder_ld_r1__r2),
    .ADD_R1__R2(Instruction_Decoder_add_r1__r2), .LD_R1__data(Instruction_Decoder_ld_r1__data),
    .ADD_R1__data(Instruction_Decoder_add_r1__data), .SUB_R1__data(Instruction_Decoder_sub_r1__data),
    .JP(Instruction_Decoder_jp));  // open: SUB_R1__R2, JP_Z
  assign out_15 = decoder_2_out1 ? out_14[7:2] : 6'bz;  // Controlled_Buffer controlled_buffer_7
  or or_4 (or_4_out, Instruction_Decoder_ld_r1__data, Instruction_Decoder_add_r1__data, Instruction_Decoder_sub_r1__data);
  or or_5 (or_5_out, Instruction_Decoder_ld_r1__r2, Instruction_Decoder_add_r1__r2);
  Register IR (.D(To_IR), .Q(IR_q), .clk(and_1_out), .clr(Reset));  // open: en
  assign out_13 = {{7{decoder_2_out1}}, decoder_2_out1};  // Bit_Extender bit_extender_2
  assign out_14 = out_13 & IR_q;  // AND_Gate and_4, 8 bits wide
  Decoder #(.select(2), .disabled(0)) decoder_3 (
    .out0(decoder_3_out0), .out1(decoder_3_out1), .out2(decoder_3_out2), .out3(decoder_3_out3),
    .sel(out_14[5:4]), .en(or_4_out));
  Decoder #(.disabled(0)) decoder_4 (.out0(decoder_4_out0), .out1(decoder_4_out1), .sel(out_14[0]), .en(or_5_out));
  Decoder #(.disabled(0)) decoder_5 (.out0(decoder_5_out0), .out1(decoder_5_out1), .sel(out_14[1]), .en(or_5_out));
  assign bit_extender_3_out = {{3{Instruction_Decoder_ld_r1__data}}, Instruction_Decoder_ld_r1__data};  // Bit_Extender bit_extender_3
  assign and_5_out = bit_extender_3_out & out_14[3:0];  // AND_Gate and_5, 4 bits wide
  and and_6 (and_6_out, decoder_3_out0, Instruction_Decoder_ld_r1__data);
  assign controlled_buffer_8_out = decoder_4_out0 ? controlled_buffer_24_out : 4'bz;  // Controlled_Buffer controlled_buffer_8
  and and_7 (and_7_out, decoder_3_out1, Instruction_Decoder_ld_r1__data);
  assign controlled_buffer_9_out = decoder_4_out1 ? controlled_buffer_24_out : 4'bz;  // Controlled_Buffer controlled_buffer_9
  and and_8 (and_8_out, decoder_3_out2, Instruction_Decoder_ld_r1__data);
  and and_9 (and_9_out, decoder_3_out3, Instruction_Decoder_ld_r1__data);
  or or_6 (or_6_out, Instruction_Decoder_add_r1__data, Instruction_Decoder_ld_r1__r2, Instruction_Decoder_add_r1__r2, Instruction_Decoder_sub_r1__data, Instruction_Decoder_ld_r1__data);
  and and_10 (and_10_out, or_6_out, and_11_out);
  assign controlled_buffer_10_out = Instruction_Decoder_add_r1__data ? out_18 : 4'bz;  // Controlled_Buffer controlled_buffer_10
  assign controlled_buffer_8_out = and_6_out ? and_5_out : 4'bz;  // Controlled_Buffer controlled_buffer_11
  assign controlled_buffer_9_out = and_7_out ? and_5_out : 4'bz;  // Controlled_Buffer controlled_buffer_12
  assign controlled_buffer_13_out = and_8_out ? and_5_out : 4'bz;  // Controlled_Buffer controlled_buffer_13
  assign controlled_buffer_14_out = and_9_out ? and_5_out : 4'bz;  // Controlled_Buffer controlled_buffer_14
  and and_11 (and_11_out, CLK_B, decoder_2_out1);
  assign controlled_buffer_10_out = Instruction_Decoder_sub_r1__data ? out_19 : 4'bz;  // Controlled_Buffer controlled_buffer_15
  assign controlled_buffer_8_out = decoder_3_out0 ? controlled_buffer_10_out : 4'bz;  // Controlled_Buffer controlled_buffer_16
  assign controlled_buffer_9_out = decoder_3_out1 ? controlled_buffer_10_out : 4'bz;  // Controlled_Buffer controlled_buffer_17
  assign controlled_buffer_13_out = decoder_3_out2 ? controlled_buffer_10_out : 4'bz;  // Controlled_Buffer controlled_buffer_18
  assign controlled_buffer_14_out = decoder_3_out3 ? controlled_buffer_10_out : 4'bz;  // Controlled_Buffer controlled_buffer_19
  assign controlled_buffer_20_out = decoder_3_out0 ? Register_A_q : 4'bz;  // Controlled_Buffer controlled_buffer_20
  Register #(.width(4)) Register_A (
    .D(controlled_buffer_8_out), .en(1'b1), .Q(Register_A_q), .clk(and_10_out), .clr(Reset));
  assign controlled_buffer_20_out = decoder_3_out1 ? Register_B_q : 4'bz;  // Controlled_Buffer controlled_buffer_21
  Register #(.width(4)) Register_B (
    .D(controlled_buffer_9_out), .en(1'b1), .Q(Register_B_q), .clk(and_10_out), .clr(Reset));
  Register #(.width(4), .trigger("falling")) Register_C (
    .D(controlled_buffer_13_out), .en(1'b1), .Q(Register_C_q), .clk(and_10_out), .clr(Reset));
  assign controlled_buffer_20_out = decoder_3_out2 ? Register_C_q : 4'bz;  // Controlled_Buffer controlled_buffer_22
  Register #(.width(4), .trigger("falling")) Register_D (
    .D(controlled_buffer_14_out), .en(1'b1), .Q(Register_D_q), .clk(and_10_out), .clr(Reset));
  assign controlled_buffer_20_out = decoder_3_out3 ? Register_D_q : 4'bz;  // Controlled_Buffer controlled_buffer_23
  assign controlled_buffer_24_out = decoder_5_out0 ? Register_C_q : 4'bz;  // Controlled_Buffer controlled_buffer_24
  assign controlled_buffer_24_out = decoder_5_out1 ? Register_D_q : 4'bz;  // Controlled_Buffer controlled_buffer_25
  Adder #(.width(4)) adder_3 (.a(controlled_buffer_20_out), .b(out_14[3:0]), .out(out_18), .cin(1'b0));  // open: cout
  Subtractor #(.width(4)) subtractor_1 (
    .a(controlled_buffer_20_out), .b(out_14[3:0]), .out(out_19), .bin(1'b0));  // open: bout
  Adder #(.width(4)) adder_4 ();  // open: a, b, out, cin, cout
  assign controlled_buffer_26_out = Instruction_Decoder_add_r1__r2 ? undriven_2 : 4'bz;  // Controlled_Buffer controlled_buffer_26

  assign out_17 = out_14[3:0];
  assign out_20 = in_5[0];
  assign out_21 = in_5[1];
  assign out_22 = in_5[2];
  assign out_23 = in_5[3];
  assign out_28 = in_5[4];
  assign out_29 = {out_24, out_25, out_26};
  assign out_30 = in_5[5];

  // Notes on the sheet:
  //   Fetch
  //   Execute
  //   JP addr
  //   ADD R1, data
  //   SUB R1, data
  //   LD R1, data
  //   ADD R1, R2
  //   LD R1, R2
  //   Register selection for imediate instructions
  //   Register selection for BY Register instructions
  //   First register (A or B)
  //   Second register (C or D)
  //   Data for imediate instructions
  //   or address for direct instructions
endmodule
