// Logisim project 4 bit cpu v1.2.1.circ as structural Verilog: 1 circuit, main circuit main
module main (
  input  in_1,
  input  [3:0] in_2,
  input  [3:0] in_3,
  input  [3:0] in_4,
  input  [7:0] in_5,
  output [3:0] out_6,
  output [7:0] Memory_Out,
  output [3:0] out_8,
  output [3:0] out_9,
  output [3:0] out_10,
  output CLK_A,
  output [3:0] out_12,
  output [7:0] out_13,
  output [7:0] out_14,
  output [5:0] out_15,
  output CLK_B,
  output [3:0] out_17,
  output [3:0] out_18,
  output [3:0] out_19,
  output out_20,
  output out_21,
  output out_22,
  output out_23,
  output [1:0] out_24,
  output [1:0] out_25,
  output [1:0] out_26,
  output [1:0] out_27,
  output out_28,
  output [5:0] out_29,
  output out_30,
  output out_31
);

  wire ALU_B_Imediate_mode_enable, ALU_Z_flag, and_1_out, and_2_out, and_3_out, and_7_out, and_8_out,
       and_9_out, and_10_out, and_11_out, and_12_out, and_13_out, button_1_out, button_2_out, button_3_out,
       clock_1_out, clock_2_out, decoder_1_out0, decoder_2_out0, decoder_2_out1, decoder_2_out2,
       decoder_3_out0, decoder_3_out1, decoder_4_out0, decoder_4_out1, decoder_4_out2, decoder_4_out3,
       decoder_5_out0, decoder_5_out1, Instruction_Decoder_add_r1__data, Instruction_Decoder_add_r1__r2,
       Instruction_Decoder_jp__addr, Instruction_Decoder_jp_z___addr, Instruction_Decoder_ld_a___addr,
       Instruction_Decoder_ld_r1__data, Instruction_Decoder_ld_r1__r2, Instruction_Decoder_st__addr___a,
       Instruction_Decoder_sub_r1__data, Instruction_Decoder_sub_r1__r2, nor_1_out, or_2_out, or_3_out,
       or_4_out, or_6_out, or_7_out, or_8_out, or_9_out, or_10_out, or_11_out, or_12_out, or_13_out,
       or_14_out, Reset, undriven;
  wire [1:0] counter_1_q, counter_2_q;
  wire [3:0] adder_2_out, ALU_A_input, ALU_B_input, and_6_out, bit_extender_3_out, controlled_buffer_3_out,
       controlled_buffer_11_out, controlled_buffer_14_out, controlled_buffer_15_out,
       controlled_buffer_18_out, controlled_buffer_21_out, controlled_buffer_22_out,
       controlled_buffer_34_out, controlled_buffer_36_out, controlled_buffer_39_out, PC_q, Reg_A_out,
       Reg_B_out, Reg_C_out, Reg_D_out;
  wire [7:0] IR_q;

  Button button_1 (.out(button_1_out));
  assign out_9 = button_2_out ? in_4 : 4'bz;  // Controlled_Buffer controlled_buffer_1
  Button button_2 (.out(button_2_out));
  Decoder #(.select(2)) decoder_1 (
    .out0(decoder_1_out0), .out1(CLK_B), .sel(counter_1_q), .en(1'b1));  // open: out2, out3
  Counter #(.width(2), .max('h3)) counter_1 (
    .load(1'b0), .count(1'b1), .Q(counter_1_q), .clk(clock_1_out), .clr(Reset));  // open: D, carry
  Clock clock_1 (.out(clock_1_out));
  LED led_1 (.in(in_1));
  LED led_2 (.in(button_1_out));
  Clock clock_2 (.out(clock_2_out));
  or or_1 (CLK_A, decoder_1_out0, CLK_B);
  LED Led1 (.in(clock_2_out));
  Controlled_Buffer controlled_buffer_2 ();  // open: in, out, en
  Counter #(.width(2), .max('h3)) counter_2 (
    .Q(counter_2_q), .clk(CLK_A), .clr(or_2_out));  // open: load, D, count, carry
  or or_2 (or_2_out, decoder_2_out2, Reset);
  Decoder #(.select(2)) decoder_2 (
    .out0(decoder_2_out0), .out1(decoder_2_out1), .out2(decoder_2_out2), .sel(counter_2_q));  // open: out3, en
  LED led_3 (.in(Reset));
  Button u_Reset (.out(Reset));
  Adder #(.width(4)) adder_1 (.a(in_2), .b(in_3), .out(out_8));  // open: cin, cout
  Adder #(.width(4)) adder_2 (.a(PC_q), .b(4'b0001), .out(adder_2_out), .cin(1'b0));  // open: cout
  and and_1 (and_1_out, decoder_2_out0, CLK_B);
  assign controlled_buffer_3_out = decoder_2_out0 ? adder_2_out : 4'bz;  // Controlled_Buffer controlled_buffer_3
  Hex_Digit_Display hex_digit_display_1 (.value(out_8), .dp(button_3_out));
  Button button_3 (.out(button_3_out));
  or or_3 (or_3_out, and_1_out, and_2_out);
  assign controlled_buffer_3_out = or_4_out ? out_14[3:0] : 4'bz;  // Controlled_Buffer controlled_buffer_4
  Register #(.width(4)) PC (.D(controlled_buffer_3_out), .en(1'b1), .Q(PC_q), .clk(or_3_out), .clr(Reset));
  and and_2 (and_2_out, CLK_B, or_4_out);
  assign out_12 = {{3{decoder_2_out0}}, decoder_2_out0};  // Bit_Extender bit_extender_1
  or or_4 (or_4_out, Instruction_Decoder_jp__addr, and_3_out);
  and and_3 (and_3_out, ALU_Z_flag, Instruction_Decoder_jp_z___addr);
  or or_5 (ALU_B_Imediate_mode_enable, Instruction_Decoder_add_r1__data, Instruction_Decoder_sub_r1__data);
  assign out_10 = PC_q & out_12;  // AND_Gate and_4, 4 bits wide
  assign out_6 = decoder_2_out0 ? out_10 : 4'bz;  // Controlled_Buffer controlled_buffer_5
  assign out_6 = Instruction_Decoder_ld_a___addr ? {1'b1, out_14[2:0]} : 4'bz;  // Controlled_Buffer controlled_buffer_6
  assign out_31 = undriven ? 1'b1 : 1'bz;  // Controlled_Buffer controlled_buffer_7
  Button button_4 ();  // open: out
  or or_6 (or_6_out, Instruction_Decoder_ld_a___addr, Instruction_Decoder_st__addr___a, decoder_2_out0);
  RAM #(.addrWidth(4), .bus("asynch")) ram_1 (
    .addr(out_6), .data(Memory_Out), .sel(or_6_out), .ld(or_7_out), .clr(1'b0));
  or or_7 (or_7_out, Instruction_Decoder_ld_a___addr, decoder_2_out0);
  intruction_decoder_2_main Instruction_Decoder (
    .Chip_Enable(decoder_2_out1), .Input(out_15), .LD_R1__R2(Instruction_Decoder_ld_r1__r2),
    .ADD_R1__R2(Instruction_Decoder_add_r1__r2), .LD_R1__data(Instruction_Decoder_ld_r1__data),
    .SUB_R1__R2(Instruction_Decoder_sub_r1__r2), .ADD_R1__data(Instruction_Decoder_add_r1__data),
    .SUB_R1__data(Instruction_Decoder_sub_r1__data), .JP__addr(Instruction_Decoder_jp__addr),
    .JP_Z___addr(Instruction_Decoder_jp_z___addr), .LD_A___addr(Instruction_Decoder_ld_a___addr),
    .ST__addr___A(Instruction_Decoder_st__addr___a));
  assign out_15 = decoder_2_out1 ? out_14[7:2] : 6'bz;  // Controlled_Buffer controlled_buffer_8
  or or_8 (or_8_out, Instruction_Decoder_ld_r1__data, Instruction_Decoder_add_r1__data, Instruction_Decoder_sub_r1__data);
  or or_9 (or_9_out, Instruction_Decoder_ld_r1__r2, Instruction_Decoder_add_r1__r2, Instruction_Decoder_sub_r1__r2);
  Decoder #(.disabled(0)) decoder_3 (.out0(decoder_3_out0), .out1(decoder_3_out1), .sel(out_14[0]), .en(or_9_out));
  or or_10 (or_10_out, Instruction_Decoder_add_r1__r2, Instruction_Decoder_sub_r1__r2);
  Register IR (.D(Memory_Out), .Q(IR_q), .clk(and_1_out), .clr(Reset));  // open: en
  assign out_13 = {{7{decoder_2_out1}}, decoder_2_out1};  // Bit_Extender bit_extender_2
  assign out_14 = out_13 & IR_q;  // AND_Gate and_5, 8 bits wide
  Decoder #(.select(2), .disabled(0)) decoder_4 (
    .out0(decoder_4_out0), .out1(decoder_4_out1), .out2(decoder_4_out2), .out3(decoder_4_out3),
    .sel(out_14[5:4]), .en(or_8_out));
  Decoder #(.disabled(0)) decoder_5 (.out0(decoder_5_out0), .out1(decoder_5_out1), .sel(out_14[1]), .en(or_9_out));
  assign ALU_A_input = decoder_5_out0 ? Reg_A_out : 4'bz;  // Controlled_Buffer controlled_buffer_9
  assign ALU_A_input = decoder_5_out1 ? Reg_B_out : 4'bz;  // Controlled_Buffer controlled_buffer_10
  assign bit_extender_3_out = {{3{Instruction_Decoder_ld_r1__data}}, Instruction_Decoder_ld_r1__data};  // Bit_Extender bit_extender_3
  assign controlled_buffer_11_out = decoder_3_out1 ? Reg_D_out : 4'bz;  // Controlled_Buffer controlled_buffer_11
  assign ALU_B_input = or_10_out ? controlled_buffer_11_out : 4'bz;  // Controlled_Buffer controlled_buffer_12
  assign out_6 = Instruction_Decoder_st__addr___a ? out_14[3:0] : 4'bz;  // Controlled_Buffer controlled_buffer_13
  assign and_6_out = bit_extender_3_out & out_14[3:0];  // AND_Gate and_6, 4 bits wide
  and and_7 (and_7_out, decoder_4_out0, Instruction_Decoder_ld_r1__data);
  assign controlled_buffer_14_out = decoder_5_out0 ? controlled_buffer_36_out : 4'bz;  // Controlled_Buffer controlled_buffer_14
  and and_8 (and_8_out, decoder_4_out1, Instruction_Decoder_ld_r1__data);
  assign controlled_buffer_15_out = decoder_5_out1 ? controlled_buffer_36_out : 4'bz;  // Controlled_Buffer controlled_buffer_15
  and and_9 (and_9_out, decoder_4_out2, Instruction_Decoder_ld_r1__data);
  and and_10 (and_10_out, decoder_4_out3, Instruction_Decoder_ld_r1__data);
  assign controlled_buffer_11_out = decoder_3_out0 ? Reg_C_out : 4'bz;  // Controlled_Buffer controlled_buffer_16
  assign Memory_Out = Instruction_Decoder_st__addr___a ? {4'b0000, Reg_A_out} : 8'bz;  // Controlled_Buffer controlled_buffer_17
  or or_11 (or_11_out, Instruction_Decoder_add_r1__data, Instruction_Decoder_ld_r1__r2, Instruction_Decoder_add_r1__r2, Instruction_Decoder_ld_a___addr, Instruction_Decoder_sub_r1__r2, Instruction_Decoder_sub_r1__data, Instruction_Decoder_ld_r1__data);
  and and_11 (and_11_out, or_11_out, and_12_out);
  assign controlled_buffer_18_out = Instruction_Decoder_add_r1__data ? out_18 : 4'bz;  // Controlled_Buffer controlled_buffer_18
  assign controlled_buffer_14_out = and_7_out ? and_6_out : 4'bz;  // Controlled_Buffer controlled_buffer_19
  assign controlled_buffer_15_out = and_8_out ? and_6_out : 4'bz;  // Controlled_Buffer controlled_buffer_20
  assign controlled_buffer_21_out = and_9_out ? and_6_out : 4'bz;  // Controlled_Buffer controlled_buffer_21
  assign controlled_buffer_22_out = and_10_out ? and_6_out : 4'bz;  // Controlled_Buffer controlled_buffer_22
  and and_12 (and_12_out, CLK_B, decoder_2_out1);
  assign controlled_buffer_18_out = Instruction_Decoder_sub_r1__data ? out_19 : 4'bz;  // Controlled_Buffer controlled_buffer_23
  assign controlled_buffer_14_out = decoder_4_out0 ? controlled_buffer_18_out : 4'bz;  // Controlled_Buffer controlled_buffer_24
  assign controlled_buffer_15_out = decoder_4_out1 ? controlled_buffer_18_out : 4'bz;  // Controlled_Buffer controlled_buffer_25
  assign controlled_buffer_21_out = decoder_4_out2 ? controlled_buffer_18_out : 4'bz;  // Controlled_Buffer controlled_buffer_26
  assign controlled_buffer_22_out = decoder_4_out3 ? controlled_buffer_18_out : 4'bz;  // Controlled_Buffer controlled_buffer_27
  assign controlled_buffer_14_out = Instruction_Decoder_ld_a___addr ? Memory_Out[3:0] : 4'bz;  // Controlled_Buffer controlled_buffer_28
  Register #(.width(4)) Register_A (
    .D(controlled_buffer_14_out), .en(1'b1), .Q(Reg_A_out), .clk(and_11_out), .clr(Reset));
  Register #(.width(4)) Register_B (
    .D(controlled_buffer_15_out), .en(1'b1), .Q(Reg_B_out), .clk(and_11_out), .clr(Reset));
  Register #(.width(4)) Register_C (
    .D(controlled_buffer_21_out), .en(1'b1), .Q(Reg_C_out), .clk(and_11_out), .clr(Reset));
  Register #(.width(4)) Register_D (
    .D(controlled_buffer_22_out), .en(1'b1), .Q(Reg_D_out), .clk(and_11_out), .clr(Reset));
  assign ALU_B_input = ALU_B_Imediate_mode_enable ? out_14[3:0] : 4'bz;  // Controlled_Buffer controlled_buffer_29
  assign ALU_A_input = decoder_4_out0 ? Reg_A_out : 4'bz;  // Controlled_Buffer controlled_buffer_30
  assign ALU_A_input = decoder_4_out1 ? Reg_B_out : 4'bz;  // Controlled_Buffer controlled_buffer_31
  assign ALU_A_input = decoder_4_out2 ? Reg_C_out : 4'bz;  // Controlled_Buffer controlled_buffer_32
  assign ALU_A_input = decoder_4_out3 ? Reg_D_out : 4'bz;  // Controlled_Buffer controlled_buffer_33
  Adder #(.width(4)) adder_3 (.a(ALU_A_input), .b(ALU_B_input), .out(out_18), .cin(1'b0));  // open: cout
  Subtractor #(.width(4)) subtractor_1 (.a(ALU_A_input), .b(ALU_B_input), .out(out_19), .bin(1'b0));  // open: bout
  assign controlled_buffer_34_out = decoder_3_out0 ? Reg_C_out : 4'bz;  // Controlled_Buffer controlled_buffer_34
  assign controlled_buffer_34_out = decoder_3_out1 ? Reg_D_out : 4'bz;  // Controlled_Buffer controlled_buffer_35
  assign controlled_buffer_36_out = Instruction_Decoder_add_r1__r2 ? out_18 : 4'bz;  // Controlled_Buffer controlled_buffer_36
  assign controlled_buffer_36_out = Instruction_Decoder_ld_r1__r2 ? controlled_buffer_34_out : 4'bz;  // Controlled_Buffer controlled_buffer_37
  or or_12 (or_12_out, Instruction_Decoder_add_r1__data, Instruction_Decoder_add_r1__r2);
  assign controlled_buffer_36_out = Instruction_Decoder_sub_r1__r2 ? out_19 : 4'bz;  // Controlled_Buffer controlled_buffer_38
  assign controlled_buffer_39_out = or_12_out ? out_18 : 4'bz;  // Controlled_Buffer controlled_buffer_39
  assign controlled_buffer_39_out = or_14_out ? out_19 : 4'bz;  // Controlled_Buffer controlled_buffer_40
  or or_13 (or_13_out, or_12_out, or_14_out);
  or or_14 (or_14_out, Instruction_Decoder_sub_r1__data, Instruction_Decoder_sub_r1__r2);
  and and_13 (and_13_out, CLK_B, or_13_out);
  nor nor_1 (nor_1_out, controlled_buffer_39_out[0], controlled_buffer_39_out[1], controlled_buffer_39_out[2], controlled_buffer_39_out[3]);
  D_Flip_Flop u_ALU_Z_flag (
    .clk(and_13_out), .D(nor_1_out), .Q(ALU_Z_flag), .preset(1'b0), .en(1'b1), .reset(Reset));  // open: Qn

  assign out_17 = out_14[3:0];
  assign out_20 = in_5[0];
  assign out_21 = in_5[1];
  assign out_22 = in_5[2];
  assign out_23 = in_5[3];
  assign out_26 = out_25;
  assign out_28 = in_5[4];
  assign out_29 = {out_24, out_25, out_25};
  assign out_30 = in_5[5];

  // Notes on the sheet:
  //   Fetch
  //   Execute
  //   JP [addr]
  //   ST [addr], A
  //   LD A, [addr]
  //   JP Z, [addr]
  //   SUB R1, data
  //   LD R1, data
  //   ADD R1, data
  //   ADD R1, R2
  //   SUB R1, R2
  //   LD R1, R2
  //   Register selection for imediate instructions
  //   Register selection for BY Register instructions
  //   First register (A or B)
  //   Second register (C or D)
  //   Data for imediate instructions
  //   or address for direct instructions
  //   JACA-1 - 4-bit Homebrew CPU
  //   v. 1.2.1
  //   https://hackaday.io/project/24511-jaca-1-homebrew-cpu
endmodule
