// Logisim project 4 bit cpu 18-04-2017.circ as structural Verilog: 1 circuit, main circuit main
module main (
  input  in_1,
  input  [3:0] in_2,
  input  [3:0] in_3,
  input  [3:0] in_4,
  input  [3:0] in_5,
  input  Fetch,
  output [3:0] out_7,
  output [3:0] out_8,
  output [3:0] out_9,
  output [7:0] To_IR,
  output [3:0] out_11,
  output [3:0] out_12
);

  wire button_1_out, button_2_out, button_3_out, button_4_out, clock_1_out;
  wire [3:0] PC_q;

  Button button_1 (.out(button_1_out));
  LED led_1 (.in(in_1));
  LED led_2 (.in(button_1_out));
  Clock clock_1 (.out(clock_1_out));
  LED Led1 (.in(clock_1_out));
  Controlled_Buffer controlled_buffer_1 (.in(clock_1_out));  // open: out, en
  assign out_9 = button_2_out ? in_4 : 4'bz;  // Controlled_Buffer controlled_buffer_2
  Button button_2 (.out(button_2_out));
  Adder #(.width(4)) adder_1 (.a(in_2), .b(in_3), .out(out_7));  // open: cin, cout
  Hex_Digit_Display hex_digit_display_1 (.value(out_7), .dp(button_3_out));
  Button button_3 (.out(button_3_out));
  Button button_4 (.out(button_4_out));
  Register #(.width(4)) PC (.D(in_5), .Q(PC_q), .clk(button_4_out));  // open: en, clr
  assign out_12 = {{3{Fetch}}, Fetch};  // Bit_Extender bit_extender_1
  assign out_11 = PC_q & out_12;  // AND_Gate and_1, 4 bits wide
  assign out_8 = Fetch ? out_11 : 4'bz;  // Controlled_Buffer controlled_buffer_3
  RAM #(.addrWidth(4), .bus("asynch")) ram_1 (.addr(out_8), .data(To_IR), .sel(Fetch), .ld(1'b1), .clr(1'b0));
endmodule
