// Logisim project 4 bit cpu a.circ as structural Verilog: 1 circuit, main circuit main
module main (
  input  in_1,
  input  [3:0] in_2,
  input  [3:0] in_3,
  input  [3:0] in_4,
  input  [3:0] in_5,
  input  Fetch,
  input  Execute,
  input  [7:0] in_8,
  output [3:0] out_9,
  output [3:0] out_10,
  output [7:0] To_IR,
  output [3:0] out_12,
  output [3:0] out_13,
  output [3:0] out_14,
  output out_15,
  output [7:0] out_16,
  output out_17,
  output out_18,
  output [7:0] out_19,
  output out_20,
  output out_21,
  output [5:0] out_22,
  output out_23,
  output [3:0] out_24,
  output [1:0] out_25,
  output [1:0] out_26,
  output [1:0] out_27,
  output [1:0] out_28,
  output [5:0] out_29,
  output [3:0] out_30
);

  wire and_4_out, buffer_1_out, buffer_2_out, button_1_out, button_2_out, button_3_out, button_4_out,
       clock_1_out, decoder_1_out0, decoder_1_out1, decoder_1_out2, decoder_1_out3,
       Instruction_Decoder_add_r1__data, Instruction_Decoder_jp_z, Instruction_Decoder_ld_r1__data, or_1_out;
  wire [3:0] and_3_out, and_5_out, and_6_out, and_7_out, bit_extender_3_out, bit_extender_4_out,
       bit_extender_5_out, bit_extender_6_out, controlled_buffer_5_out, controlled_buffer_7_out, PC_q,
       Register_A_q;
  wire [7:0] IR_q;

  Button button_1 (.out(button_1_out));
  LED led_1 (.in(in_1));
  LED led_2 (.in(button_1_out));
  Clock clock_1 (.out(clock_1_out));
  LED Led1 (.in(clock_1_out));
  Controlled_Buffer controlled_buffer_1 (.in(clock_1_out));  // open: out, en
  assign out_12 = button_2_out ? in_4 : 4'bz;  // Controlled_Buffer controlled_buffer_2
  Button button_2 (.out(button_2_out));
  Adder #(.width(4)) adder_1 (.a(in_2), .b(in_3), .out(out_9));  // open: cin, cout
  Hex_Digit_Display hex_digit_display_1 (.value(out_9), .dp(button_3_out));
  Button button_3 (.out(button_3_out));
  Button button_4 (.out(button_4_out));
  Register #(.width(4), .trigger("falling")) PC (.D(in_5), .Q(PC_q), .clk(button_4_out));  // open: en, clr
  assign out_14 = {{3{Fetch}}, Fetch};  // Bit_Extender bit_extender_1
  assign out_13 = PC_q & out_14;  // AND_Gate and_1, 4 bits wide
  assign out_10 = Fetch ? out_13 : 4'bz;  // Controlled_Buffer controlled_buffer_3
  RAM #(.addrWidth(4), .bus("asynch")) ram_1 (.addr(out_10), .data(To_IR), .sel(Fetch), .ld(1'b1), .clr(1'b0));
  intruction_decoder_2_main Instruction_Decoder (
    .Chip_Enable(Execute), .Input(out_22), .LD_R1__data(Instruction_Decoder_ld_r1__data),
    .ADD_R1__data(Instruction_Decoder_add_r1__data), .JP_Z(Instruction_Decoder_jp_z));  // open: LD_R1__R2, ADD_R1__R2, SUB_R1__R2, SUB_R1__data, JP
  assign out_22 = Execute ? out_19[7:2] : 6'bz;  // Controlled_Buffer controlled_buffer_4
  Register #(.trigger("falling")) IR (.D(To_IR), .Q(IR_q), .clk(Fetch), .clr(1'b0));  // open: en
  assign out_16 = {{7{Execute}}, Execute};  // Bit_Extender bit_extender_2
  assign out_19 = out_16 & IR_q;  // AND_Gate and_2, 8 bits wide
  Decoder #(.select(2)) decoder_1 (
    .out0(decoder_1_out0), .out1(decoder_1_out1), .out2(decoder_1_out2), .out3(decoder_1_out3),
    .sel(out_19[5:4]), .en(1'b1));
  assign bit_extender_3_out = {{3{Instruction_Decoder_ld_r1__data}}, Instruction_Decoder_ld_r1__data};  // Bit_Extender bit_extender_3
  assign bit_extender_4_out = {{3{decoder_1_out1}}, decoder_1_out1};  // Bit_Extender bit_extender_4
  assign bit_extender_5_out = {{3{decoder_1_out2}}, decoder_1_out2};  // Bit_Extender bit_extender_5
  assign bit_extender_6_out = {{3{decoder_1_out3}}, decoder_1_out3};  // Bit_Extender bit_extender_6
  assign and_3_out = bit_extender_3_out & out_19[3:0];  // AND_Gate and_3, 4 bits wide
  and and_4 (and_4_out, decoder_1_out0, Instruction_Decoder_ld_r1__data);
  or or_1 (or_1_out, Instruction_Decoder_add_r1__data, Instruction_Decoder_ld_r1__data);
  assign controlled_buffer_5_out = Instruction_Decoder_add_r1__data ? out_30 : 4'bz;  // Controlled_Buffer controlled_buffer_5
  assign controlled_buffer_5_out = and_4_out ? and_3_out : 4'bz;  // Controlled_Buffer controlled_buffer_6
  assign and_5_out = bit_extender_4_out & and_3_out;  // AND_Gate and_5, 4 bits wide
  assign and_6_out = bit_extender_5_out & and_3_out;  // AND_Gate and_6, 4 bits wide
  assign and_7_out = bit_extender_6_out & and_3_out;  // AND_Gate and_7, 4 bits wide
  buf buffer_1 (buffer_1_out, or_1_out);
  buf buffer_2 (buffer_2_out, buffer_1_out);
  Register #(.width(4), .trigger("falling")) Register_A (
    .D(controlled_buffer_5_out), .en(1'b1), .Q(Register_A_q), .clk(buffer_2_out));  // open: clr
  Register #(.width(4), .trigger("falling")) Register_B (.D(and_5_out), .clk(buffer_2_out));  // open: en, Q, clr
  Register #(.width(4), .trigger("falling")) Register_C (.D(and_6_out), .clk(buffer_2_out));  // open: en, Q, clr
  Register #(.width(4), .trigger("falling")) Register_D (.D(and_7_out), .clk(buffer_2_out));  // open: en, Q, clr
  assign controlled_buffer_7_out = decoder_1_out0 ? Register_A_q : 4'bz;  // Controlled_Buffer controlled_buffer_7
  Adder #(.width(4)) adder_2 (.a(controlled_buffer_7_out), .b(out_19[3:0]), .out(out_30), .cin(1'b0));  // open: cout
  Adder #(.width(4)) adder_3 ();  // open: a, b, out, cin, cout

  assign out_15 = in_8[0];
  assign out_17 = in_8[1];
  assign out_18 = in_8[2];
  assign out_20 = in_8[3];
  assign out_21 = in_8[4];
  assign out_23 = in_8[5];
  assign out_24 = out_19[3:0];
  assign out_29 = {out_25, out_26, out_27};

  // Notes on the sheet:
  //   ADD R1, data
  //   LD R1, data
  //   Register selection for direct instructions
  //   Data for direct instructions
endmodule
