// Logisim project intruction decoder 2.circ as structural Verilog: 1 circuit, main circuit main
module main (
  input  Chip_Enable,
  input  [5:0] Input,
  output LD_R1__R2,
  output ADD_R1__R2,
  output LD_R1__data,
  output SUB_R1__R2,
  output ADD_R1__data,
  output SUB_R1__data,
  output JP,
  output JP_Z
);

  wire and_4_out, decoder_1_out0, decoder_1_out1, decoder_1_out2, decoder_1_out3, decoder_2_out0,
       decoder_2_out2, decoder_2_out3, decoder_3_out0, decoder_3_out1, decoder_3_out2;

  Decoder #(.select(2)) decoder_1 (
    .out0(decoder_1_out0), .out1(decoder_1_out1), .out2(decoder_1_out2), .out3(decoder_1_out3),
    .sel(Input[5:4]), .en(1'b1));
  and and_1 (LD_R1__data, decoder_1_out0, Chip_Enable);
  and and_2 (ADD_R1__data, decoder_1_out1, Chip_Enable);
  and and_3 (SUB_R1__data, decoder_1_out2, Chip_Enable);
  Decoder #(.select(2)) decoder_2 (
    .out0(decoder_2_out0), .out2(decoder_2_out2), .out3(decoder_2_out3), .sel(Input[3:2]), .en(1'b1));  // open: out1
  and and_4 (and_4_out, decoder_1_out3, decoder_2_out0, Chip_Enable);
  Decoder #(.select(2)) decoder_3 (
    .out0(decoder_3_out0), .out1(decoder_3_out1), .out2(decoder_3_out2), .sel(Input[1:0]), .en(1'b1));  // open: out3
  and and_5 (JP, decoder_1_out3, Chip_Enable, decoder_2_out3);
  and and_6 (JP_Z, decoder_1_out3, Chip_Enable, decoder_2_out2);
  and and_7 (LD_R1__R2, decoder_3_out0, and_4_out, Chip_Enable);
  and and_8 (ADD_R1__R2, decoder_3_out1, and_4_out, Chip_Enable);
  and and_9 (SUB_R1__R2, decoder_3_out2, and_4_out, Chip_Enable);

  // Notes on the sheet:
  //   Instruction Decoder
  //   PS: some outputs are open (high impedance) when CE=0, others are 0. Don't know if this will lead to a problem
endmodule
