// Logisim project clock generator.circ as structural Verilog: 1 circuit, main circuit main
module main (
  input  Clear,
  output CLK1,
  output CLK2
);

  wire clock_1_out, decoder_1_out2;
  wire [1:0] counter_1_q;

  Clock clock_1 (.out(clock_1_out));
  Decoder #(.select(2)) decoder_1 (
    .out2(decoder_1_out2), .out3(CLK2), .sel(counter_1_q), .en(1'b1));  // open: out0, out1
  Counter #(.width(2), .max('h3)) counter_1 (
    .load(1'b0), .count(1'b1), .Q(counter_1_q), .clk(clock_1_out), .clr(Clear));  // open: D, carry
  or or_1 (CLK1, decoder_1_out2, CLK2);
endmodule
