// Logisim project intruction decoder 2.circ as structural Verilog: 1 circuit, main circuit main
module main (
  input  Chip_Enable,
  input  [5:0] Input,
  output LD_R1__R2,
  output ADD_R1__R2,
  output LD_R1__data,
  output SUB_R1__R2,
  output ADD_R1__data,
  output SUB_R1__data,
  output JP__addr,
  output JP_Z___addr,
  output LD_A___addr,
  output ST__addr___A
);

  wire and_4_out, and_5_out, and_6_out, decoder_1_out0, decoder_1_out1, decoder_1_out2, decoder_1_out3,
       decoder_2_out0, decoder_2_out2, decoder_2_out3, decoder_3_out0, decoder_3_out1, decoder_3_out2,
       nor_1_out, not_1_out, not_2_out;

  Decoder #(.select(2)) decoder_1 (
    .out0(decoder_1_out0), .out1(decoder_1_out1), .out2(decoder_1_out2), .out3(decoder_1_out3),
    .sel(Input[5:4]), .en(1'b1));
  and and_1 (LD_R1__data, decoder_1_out0, and_4_out);
  and and_2 (ADD_R1__data, decoder_1_out1, and_4_out);
  and and_3 (SUB_R1__data, decoder_1_out2, and_4_out);
  and and_4 (and_4_out, Chip_Enable, nor_1_out);
  Decoder #(.select(2)) decoder_2 (
    .out0(decoder_2_out0), .out2(decoder_2_out2), .out3(decoder_2_out3), .sel(Input[3:2]), .en(1'b1));  // open: out1
  and and_5 (and_5_out, decoder_1_out3, decoder_2_out0, and_4_out);
  not not_1 (not_1_out, Input[3]);
  and and_6 (and_6_out, Input[4], Input[5], Input[2], not_1_out);
  Decoder #(.select(2)) decoder_3 (
    .out0(decoder_3_out0), .out1(decoder_3_out1), .out2(decoder_3_out2), .sel(Input[1:0]), .en(1'b1));  // open: out3
  and and_7 (JP__addr, decoder_1_out3, and_4_out, decoder_2_out3);
  and and_8 (JP_Z___addr, decoder_1_out3, and_4_out, decoder_2_out2);
  not not_2 (not_2_out, Input[1]);
  nor nor_1 (nor_1_out, ST__addr___A, LD_A___addr);
  and and_9 (LD_A___addr, not_2_out, Chip_Enable, and_6_out);
  and and_10 (ST__addr___A, and_6_out, Chip_Enable, Input[1]);
  and and_11 (LD_R1__R2, decoder_3_out0, and_5_out, and_4_out);
  and and_12 (ADD_R1__R2, decoder_3_out1, and_5_out, and_4_out);
  and and_13 (SUB_R1__R2, decoder_3_out2, and_5_out, and_4_out);

  // Notes on the sheet:
  //   Instruction Decoder
endmodule
