// Logisim project jaca-1a.circ as structural Verilog: 1 circuit, main circuit main
module main (
);

  wire clock_1_out;
  wire [3:0] ACC_q, controlled_buffer_1_out, n74181_1_p18, PC_q;
  wire [7:0] rom_1_data, rom_2_data;

  Clock clock_1 (.out(clock_1_out));
  Counter #(.width(4), .max('hf)) PC (.Q(PC_q), .clk(clock_1_out));  // open: load, D, count, carry, clr
  ROM #(.addrWidth(4)) rom_1 (.addr(PC_q), .data(rom_1_data));  // open: sel
  assign controlled_buffer_1_out = rom_2_data[7] ? rom_1_data[3:0] : 4'bz;  // Controlled_Buffer controlled_buffer_1
  ROM #(.addrWidth(4)) rom_2 (.addr(rom_1_data[7:4]), .data(rom_2_data));  // open: sel
  assign controlled_buffer_1_out = rom_2_data[6] ? n74181_1_p18 : 4'bz;  // Controlled_Buffer controlled_buffer_2
  Register #(.width(4)) ACC (.D(controlled_buffer_1_out), .Q(ACC_q));  // open: en, clk, clr
  // _74181 74181_1: pin names not known; wires that end beside it: rom_2_data[3], rom_2_data[2], rom_2_data[1], rom_2_data[0], rom_1_data[3], ACC_q[3], rom_1_data[2], ACC_q[2], rom_1_data[1], ACC_q[1], rom_1_data[0], ACC_q[0], rom_2_data[5], rom_2_data[4], n74181_1_p18[3], n74181_1_p18[2], n74181_1_p18[1], n74181_1_p18[0]

  // Notes on the sheet:
  //   RAM (AT28C256)
  //   Opcode
  //   Data
  //   Microcode Store (AT28C256)
endmodule
