// Logisim project 8-bit TTL Cpu.circ as structural Verilog: 5 circuits, main circuit main
module main (
);

  wire _74181_ALU__Hi_p14, _74181_ALU__Lo_p1, ALU_C, ALU_F0, ALU_F1, ALU_F2, ALU_F3, ALU_M,
       ALU_OUT_to_REG_IN, ALU_SHR_to_REG_IN, and_1_out, and_2_out, and_3_out, and_4_out, and_5_out,
       and_6_out, and_7_out, and_8_out, and_9_out, and_10_out, and_11_out, and_12_out, and_13_out,
       and_14_out, and_15_out, and_16_out, and_17_out, and_18_out, and_19_out, and_20_out, and_21_out,
       and_22_out, and_23_out, and_24_out, and_25_out, and_26_out, and_28_out, and_29_out, and_30_out,
       and_31_out, and_32_out, and_33_out, and_34_out, and_35_out, and_36_out, and_37_out, C_FLAG,
       C_FLAG_to_IR_ADDR_to_PC, CLK_B, clock_1_out, CLOSE_REGS_BRIDGE, d_ff_1_q, decoder_1_out4,
       decoder_2_out0, decoder_2_out1, decoder_2_out2, decoder_2_out3, decoder_2_out4, decoder_2_out5,
       decoder_2_out6, decoder_2_out7, decoder_3_out0, decoder_3_out1, decoder_3_out2, decoder_3_out3,
       decoder_3_out4, decoder_3_out5, decoder_3_out6, decoder_3_out7, demultiplexer_1_out0,
       demultiplexer_1_out1, demultiplexer_1_out2, demultiplexer_1_out3, demultiplexer_1_out4,
       demultiplexer_1_out5, demultiplexer_1_out6, demultiplexer_1_out7, EN_KBD_INPUT, EN_LED_MATRIX_OUT,
       EN_MEM, EN_R1_OUT, EN_REG_CLK, Execute, Fetch_1, Fetch_2, Fetch_3, Fetch_Any, IN_TO_R1,
       IR_ADDR_to_MEM_ADDR, IR_ADDR_to_PC, IR_DATA_to_REG_IN, MEM_DATA_to_REG_IN, MEM_READ, nand_1_out,
       nor_1_out, nor_2_out, not_3_out, not_4_out, not_5_out, or_1_out, or_2_out, or_3_out, or_4_out,
       or_6_out, or_7_out, or_8_out, or_9_out, or_10_out, or_11_out, or_12_out, OUT_REG_to_REG_IN, PC_Next,
       PC_to_REG_RET_ADDR, R1_to_MEM_DATA, R1_to_OUT, REG_RET_ADDR_to_PC, Reset, Reset_1, Reset_2, Reset_3,
       Reset_4, RR3_to_MEM_ADDR, Z_FLAG, Z_FLAG_to_IR_ADDR_to_PC;
  wire [2:0] counter_1_q, I_O_Addr, R1_Addr, R2_Addr;
  wire [5:0] OPCODE;
  wire [6:0] INPUT;
  wire [7:0] _74181_ALU__Lo_p20, A_q, ALU_A_IN, ALU_B_IN, B_q, buffer_1_out, C_q, D_q, E_q, F_q, IR_1_q,
       IR_2_q, IR_3_q, MEM_DATA, OUTPUT, REG_H_OUT, REG_IN, REG_L_OUT, register_1_q, register_2_q,
       register_3_q, register_4_q, register_5_q, register_6_q, register_7_q, register_8_q, register_9_q,
       register_10_q, register_11_q, register_12_q, register_13_q, register_14_q, register_15_q,
       register_16_q, REGS_BANK_B_OUT;
  wire [8:0] IR_Addr;
  wire [11:0] adder_1_out, controlled_buffer_1_out, controlled_buffer_4_out, PC_q, RET_ADDR_q;
  wire [31:26] rom_1_data;

  Clock clock_1 (.out(clock_1_out));
  Counter #(.width(3), .max('h7)) counter_1 (
    .count(1'b1), .Q(counter_1_q), .clk(nand_1_out), .clr(or_1_out));  // open: load, D, carry
  Pull_Resistor pull_resistor_1 (.node(ALU_A_IN));
  Pull_Resistor pull_resistor_2 (.node(ALU_B_IN));
  Decoder #(.select(3)) decoder_1 (
    .out0(Fetch_1), .out1(Fetch_2), .out2(Fetch_3), .out3(Execute), .out4(decoder_1_out4), .sel(counter_1_q),
    .en(1'b1));  // open: out5, out6, out7
  or or_1 (or_1_out, decoder_1_out4, Reset);
  and and_1 (and_1_out, nand_1_out, clock_1_out);
  D_Flip_Flop d_ff_1 (.clk(and_1_out), .D(1'b1), .Q(d_ff_1_q), .reset(Reset));  // open: Qn, preset, en
  ROM #(.addrWidth(6), .dataWidth(32)) rom_1 (
    .addr(OPCODE),
    .data({rom_1_data, ALU_SHR_to_REG_IN, IN_TO_R1, IR_DATA_to_REG_IN, EN_REG_CLK, OUT_REG_to_REG_IN, IR_ADDR_to_MEM_ADDR, EN_MEM, MEM_READ, MEM_DATA_to_REG_IN, RR3_to_MEM_ADDR, ALU_OUT_to_REG_IN, IR_ADDR_to_PC, Z_FLAG_to_IR_ADDR_to_PC, R1_to_MEM_DATA, EN_R1_OUT, CLOSE_REGS_BRIDGE, PC_to_REG_RET_ADDR, REG_RET_ADDR_to_PC, R1_to_OUT, C_FLAG_to_IR_ADDR_to_PC, ALU_F3, ALU_F2, ALU_F1, ALU_F0, ALU_M, ALU_C}));  // open: sel
  nand nand_1 (nand_1_out, clock_1_out, d_ff_1_q);
  not not_1 (Fetch_Any, Execute);
  not not_2 (CLK_B, nand_1_out);
  or or_2 (or_2_out, ALU_SHR_to_REG_IN, ALU_OUT_to_REG_IN);
  // _74181 _74181_ALU__Hi: pin names not known; wires that end beside it: ALU_F3, ALU_F2, ALU_F1, ALU_F0, ALU_B_IN[7], ALU_A_IN[7], ALU_B_IN[6], ALU_A_IN[6], ALU_B_IN[5], ALU_A_IN[5], ALU_B_IN[4], ALU_A_IN[4], ALU_M, _74181_ALU__Hi_p14, _74181_ALU__Lo_p20[7], _74181_ALU__Lo_p20[6], _74181_ALU__Lo_p20[5], _74181_ALU__Lo_p20[4]
  // _74181 _74181_ALU__Lo: pin names not known; wires that end beside it: _74181_ALU__Lo_p1, ALU_F3, ALU_F2, ALU_F1, ALU_F0, ALU_B_IN[3], ALU_A_IN[3], ALU_B_IN[2], ALU_A_IN[2], ALU_B_IN[1], ALU_A_IN[1], ALU_B_IN[0], ALU_A_IN[0], ALU_M, ALU_C, _74181_ALU__Lo_p1, _74181_ALU__Lo_p20[3], _74181_ALU__Lo_p20[2], _74181_ALU__Lo_p20[1], _74181_ALU__Lo_p20[0]
  and and_2 (and_2_out, IR_ADDR_to_PC, Execute, or_3_out);
  and and_3 (and_3_out, Z_FLAG, not_3_out);
  not not_3 (not_3_out, C_FLAG_to_IR_ADDR_to_PC);
  and and_4 (and_4_out, or_2_out, Execute, CLK_B);
  and and_5 (and_5_out, Execute, RR3_to_MEM_ADDR);
  assign controlled_buffer_1_out = and_5_out ? {REG_H_OUT[3:0], REG_L_OUT} : 12'bz;  // Controlled_Buffer controlled_buffer_1
  Adder #(.width(12)) adder_1 (.a(controlled_buffer_1_out), .b(12'h1), .out(adder_1_out), .cin(1'b0));  // open: cout
  or or_3 (or_3_out, and_3_out, nor_1_out, and_6_out);
  nor nor_1 (nor_1_out, Z_FLAG_to_IR_ADDR_to_PC, C_FLAG_to_IR_ADDR_to_PC);
  and and_6 (and_6_out, not_4_out, C_FLAG);
  not not_4 (not_4_out, Z_FLAG_to_IR_ADDR_to_PC);
  assign REG_IN = ALU_OUT_to_REG_IN ? _74181_ALU__Lo_p20 : 8'bz;  // Controlled_Buffer controlled_buffer_2
  assign REG_IN = ALU_SHR_to_REG_IN ? {1'b0, ALU_A_IN[7:1]} : 8'bz;  // Controlled_Buffer controlled_buffer_3
  assign controlled_buffer_4_out = Fetch_Any ? adder_1_out : 12'bz;  // Controlled_Buffer controlled_buffer_4
  assign controlled_buffer_4_out = and_2_out ? {I_O_Addr, IR_Addr} : 12'bz;  // Controlled_Buffer controlled_buffer_5
  and and_7 (and_7_out, and_2_out, CLK_B);
  Button u_RESET (.out(Reset_1));
  D_Flip_Flop u_C_Flag (.clk(and_4_out), .D(_74181_ALU__Hi_p14), .Q(C_FLAG), .reset(Reset));  // open: Qn, preset, en
  D_Flip_Flop u_Z_Flag (.clk(and_4_out), .D(nor_2_out), .Q(Z_FLAG), .reset(Reset));  // open: Qn, preset, en
  nor nor_2 (nor_2_out, REG_IN[0], REG_IN[1], REG_IN[2], REG_IN[3], REG_IN[4], REG_IN[5], REG_IN[6], REG_IN[7]);
  Pull_Resistor pull_resistor_3 (.node(REG_IN));
  Register #(.width(12)) PC (.D(controlled_buffer_4_out), .Q(PC_q), .clk(or_4_out), .clr(Reset));  // open: en
  or or_4 (or_4_out, and_7_out, and_8_out, PC_Next);
  and and_8 (and_8_out, REG_RET_ADDR_to_PC, CLK_B);
  and and_9 (and_9_out, Execute, CLK_B, PC_to_REG_RET_ADDR);
  Decoder #(.select(3)) decoder_2 (
    .out0(decoder_2_out0), .out1(decoder_2_out1), .out2(decoder_2_out2), .out3(decoder_2_out3),
    .out4(decoder_2_out4), .out5(decoder_2_out5), .out6(decoder_2_out6), .out7(decoder_2_out7),
    .sel(R1_Addr), .en(1'b1));
  assign controlled_buffer_4_out = REG_RET_ADDR_to_PC ? RET_ADDR_q : 12'bz;  // Controlled_Buffer controlled_buffer_6
  Register #(.width(12)) RET_ADDR (.D(PC_q), .Q(RET_ADDR_q), .clk(and_9_out), .clr(Reset));  // open: en
  and and_10 (and_10_out, IR_ADDR_to_MEM_ADDR, Execute);
  assign controlled_buffer_1_out = Fetch_Any ? PC_q : 12'bz;  // Controlled_Buffer controlled_buffer_7
  or or_5 (Reset, Reset_1, Reset_2, Reset_3, Reset_4);
  Button u_RESET_2 (.out(Reset_4));
  assign controlled_buffer_1_out = and_10_out ? {I_O_Addr, IR_Addr} : 12'bz;  // Controlled_Buffer controlled_buffer_8
  or or_6 (or_6_out, Fetch_Any, EN_MEM);
  or or_7 (or_7_out, Fetch_Any, MEM_READ);
  and and_11 (and_11_out, decoder_2_out0, EN_R1_OUT);
  and and_12 (and_12_out, decoder_2_out1, EN_R1_OUT);
  and and_13 (and_13_out, decoder_2_out2, EN_R1_OUT);
  and and_14 (and_14_out, decoder_2_out3, EN_R1_OUT);
  and and_15 (and_15_out, CLK_B, Execute, EN_REG_CLK);
  RAM #(.addrWidth(12), .bus("asynch")) ram_1 (
    .addr(controlled_buffer_1_out), .data(MEM_DATA), .sel(or_6_out), .ld(or_7_out));  // open: clr
  assign REG_IN = MEM_DATA_to_REG_IN ? MEM_DATA : 8'bz;  // Controlled_Buffer controlled_buffer_9
  assign REG_IN = IR_DATA_to_REG_IN ? IR_Addr[7:0] : 8'bz;  // Controlled_Buffer controlled_buffer_10
  and and_16 (and_16_out, decoder_2_out0, and_15_out);
  and and_17 (and_17_out, decoder_2_out1, and_15_out);
  and and_18 (and_18_out, decoder_2_out2, and_15_out);
  and and_19 (and_19_out, decoder_2_out3, and_15_out);
  and and_20 (and_20_out, decoder_2_out4, and_15_out);
  and and_21 (and_21_out, decoder_2_out5, and_15_out);
  and and_22 (and_22_out, decoder_2_out6, and_15_out);
  and and_23 (and_23_out, decoder_2_out7, and_15_out);
  assign REG_IN = IN_TO_R1 ? {1'b0, INPUT} : 8'bz;  // Controlled_Buffer controlled_buffer_11
  Register A (.D(REG_IN), .Q(A_q), .clk(and_16_out), .clr(Reset));  // open: en
  Register B (.D(REG_IN), .Q(B_q), .clk(and_17_out), .clr(Reset));  // open: en
  Register H (.D(REG_IN), .Q(REG_H_OUT), .clk(and_18_out), .clr(Reset));  // open: en
  Register L (.D(REG_IN), .Q(REG_L_OUT), .clk(and_19_out), .clr(Reset));  // open: en
  Register C (.D(REG_IN), .Q(C_q), .clk(and_20_out), .clr(Reset));  // open: en
  Register D (.D(REG_IN), .Q(D_q), .clk(and_21_out), .clr(Reset));  // open: en
  Register E (.D(REG_IN), .Q(E_q), .clk(and_22_out), .clr(Reset));  // open: en
  Register F (.D(REG_IN), .Q(F_q), .clk(and_23_out), .clr(Reset));  // open: en
  and and_24 (and_24_out, Fetch_3, CLK_B);
  and and_25 (and_25_out, Fetch_2, CLK_B);
  and and_26 (and_26_out, Fetch_1, CLK_B);
  and and_27 (PC_Next, CLK_B, Fetch_Any);
  assign IR_Addr[7:0] = Execute ? IR_3_q : 8'bz;  // Controlled_Buffer controlled_buffer_12
  Register IR_3 (.D(MEM_DATA), .Q(IR_3_q), .clk(and_24_out), .clr(Reset));  // open: en
  assign {R1_Addr[0], R2_Addr, I_O_Addr, IR_Addr[8]} = Execute ? IR_2_q : 8'bz;  // Controlled_Buffer controlled_buffer_13
  Register IR_2 (.D(MEM_DATA), .Q(IR_2_q), .clk(and_25_out), .clr(Reset));  // open: en
  Register IR_1 (.D(MEM_DATA), .Q(IR_1_q), .clk(and_26_out), .clr(Reset));  // open: en
  assign {OPCODE, R1_Addr[2:1]} = Execute ? IR_1_q : 8'bz;  // Controlled_Buffer controlled_buffer_14
  assign REG_IN = OUT_REG_to_REG_IN ? ALU_A_IN : 8'bz;  // Controlled_Buffer controlled_buffer_15
  or or_8 (or_8_out, and_11_out, and_28_out);
  assign ALU_A_IN = or_8_out ? A_q : 8'bz;  // Controlled_Buffer controlled_buffer_16
  or or_9 (or_9_out, and_12_out, and_29_out);
  assign ALU_A_IN = or_9_out ? B_q : 8'bz;  // Controlled_Buffer controlled_buffer_17
  or or_10 (or_10_out, and_13_out, and_30_out);
  assign ALU_A_IN = or_10_out ? REG_H_OUT : 8'bz;  // Controlled_Buffer controlled_buffer_18
  or or_11 (or_11_out, and_14_out, and_31_out);
  assign ALU_A_IN = or_11_out ? REG_L_OUT : 8'bz;  // Controlled_Buffer controlled_buffer_19
  assign ALU_A_IN = CLOSE_REGS_BRIDGE ? REGS_BANK_B_OUT : 8'bz;  // Controlled_Buffer controlled_buffer_20
  assign REGS_BANK_B_OUT = decoder_3_out4 ? C_q : 8'bz;  // Controlled_Buffer controlled_buffer_21
  assign REGS_BANK_B_OUT = decoder_3_out5 ? D_q : 8'bz;  // Controlled_Buffer controlled_buffer_22
  assign REGS_BANK_B_OUT = decoder_3_out6 ? E_q : 8'bz;  // Controlled_Buffer controlled_buffer_23
  assign REGS_BANK_B_OUT = decoder_3_out7 ? F_q : 8'bz;  // Controlled_Buffer controlled_buffer_24
  Pull_Resistor pull_resistor_4 (.node(IR_Addr[7:0]));
  Pull_Resistor pull_resistor_5 (.node({R1_Addr[0], R2_Addr, I_O_Addr, IR_Addr[8]}));
  Pull_Resistor pull_resistor_6 (.node({OPCODE, R1_Addr[2:1]}));
  assign MEM_DATA = R1_to_MEM_DATA ? ALU_A_IN : 8'bz;  // Controlled_Buffer controlled_buffer_25
  and and_28 (and_28_out, decoder_3_out0, not_5_out);
  and and_29 (and_29_out, decoder_3_out1, not_5_out);
  and and_30 (and_30_out, decoder_3_out2, not_5_out);
  and and_31 (and_31_out, decoder_3_out3, not_5_out);
  not not_5 (not_5_out, EN_R1_OUT);
  assign OUTPUT = R1_to_OUT ? ALU_A_IN : 8'bz;  // Controlled_Buffer controlled_buffer_26
  assign ALU_B_IN = ALU_OUT_to_REG_IN ? REGS_BANK_B_OUT : 8'bz;  // Controlled_Buffer controlled_buffer_27
  Pull_Resistor pull_resistor_7 (.node(OUTPUT));
  Decoder #(.select(3)) decoder_3 (
    .out0(decoder_3_out0), .out1(decoder_3_out1), .out2(decoder_3_out2), .out3(decoder_3_out3),
    .out4(decoder_3_out4), .out5(decoder_3_out5), .out6(decoder_3_out6), .out7(decoder_3_out7),
    .sel(R2_Addr), .en(1'b1));
  assign buffer_1_out = REGS_BANK_B_OUT;  // Buffer buffer_1, 8 bits wide
  Decoder #(.select(3)) decoder_4 (
    .out0(EN_KBD_INPUT), .out1(EN_LED_MATRIX_OUT), .sel(I_O_Addr));  // open: out2, out3, out4, out5, out6, out7, en
  and and_32 (and_32_out, OUTPUT[0], OUTPUT[1], OUTPUT[2], OUTPUT[3], OUTPUT[4], OUTPUT[5], OUTPUT[6], OUTPUT[7]);
  Register register_1 (.D(OUTPUT), .Q(register_1_q), .clk(demultiplexer_1_out0), .clr(Reset));  // open: en
  Register register_2 (.D(OUTPUT), .Q(register_2_q), .clk(demultiplexer_1_out1), .clr(Reset));  // open: en
  Pull_Resistor pull_resistor_8 (.node(buffer_1_out));
  Keyboard keyboard_1 (.clk(and_33_out), .clr(Reset), .data(INPUT));  // open: re, avail
  and and_33 (and_33_out, IN_TO_R1, CLK_B, EN_KBD_INPUT);
  Button u_RESET_3 (.out(Reset_2));
  and and_34 (and_34_out, R1_to_OUT, CLK_B, EN_KBD_INPUT);
  Register register_3 (.D(OUTPUT), .Q(register_3_q), .clk(demultiplexer_1_out2), .clr(Reset));  // open: en
  Register register_4 (.D(OUTPUT), .Q(register_4_q), .clk(demultiplexer_1_out3), .clr(Reset));  // open: en
  TTY #(.rows(2), .cols(16)) tty_1 (.data(OUTPUT[6:0]), .clk(and_34_out), .we(1'b1), .clr(or_12_out));
  or or_12 (or_12_out, Reset, and_32_out);
  Register register_5 (.D(OUTPUT), .Q(register_5_q), .clk(demultiplexer_1_out4), .clr(Reset));  // open: en
  Register register_6 (.D(OUTPUT), .Q(register_6_q), .clk(demultiplexer_1_out5), .clr(Reset));  // open: en
  Demultiplexer #(.select(3), .enable("false")) demultiplexer_1 (
    .out0(demultiplexer_1_out0), .out1(demultiplexer_1_out1), .out2(demultiplexer_1_out2),
    .out3(demultiplexer_1_out3), .out4(demultiplexer_1_out4), .out5(demultiplexer_1_out5),
    .out6(demultiplexer_1_out6), .out7(demultiplexer_1_out7), .in(and_35_out), .sel(buffer_1_out[2:0]));
  and and_35 (and_35_out, ~buffer_1_out[3], and_36_out);  // AND_Gate
  and and_36 (and_36_out, R1_to_OUT, CLK_B, EN_LED_MATRIX_OUT);
  Register register_7 (.D(OUTPUT), .Q(register_7_q), .clk(demultiplexer_1_out6), .clr(Reset));  // open: en
  Register register_8 (.D(OUTPUT), .Q(register_8_q), .clk(demultiplexer_1_out7), .clr(Reset));  // open: en
  and and_37 (and_37_out, buffer_1_out[3], and_36_out);
  Register register_9 (.D(register_1_q), .Q(register_9_q), .clk(and_37_out), .clr(Reset));  // open: en
  Register register_10 (.D(register_2_q), .Q(register_10_q), .clk(and_37_out), .clr(Reset));  // open: en
  Register register_11 (.D(register_3_q), .Q(register_11_q), .clk(and_37_out), .clr(Reset));  // open: en
  Register register_12 (.D(register_4_q), .Q(register_12_q), .clk(and_37_out), .clr(Reset));  // open: en
  Button u_RESET_4 (.out(Reset_3));
  Register register_13 (.D(register_5_q), .Q(register_13_q), .clk(and_37_out), .clr(Reset));  // open: en
  Register register_14 (.D(register_6_q), .Q(register_14_q), .clk(and_37_out), .clr(Reset));  // open: en
  Register register_15 (.D(register_7_q), .Q(register_15_q), .clk(and_37_out), .clr(Reset));  // open: en
  Register register_16 (.D(register_8_q), .Q(register_16_q), .clk(and_37_out), .clr(Reset));  // open: en
  DotMatrix #(.inputtype("row"), .matrixcols(8), .matrixrows(8)) dotmatrix_1 (
    .row0(register_9_q), .row1(register_10_q), .row2(register_11_q), .row3(register_12_q),
    .row4(register_13_q), .row5(register_14_q), .row6(register_15_q), .row7(register_16_q));

  // Other names for the same wires on the sheet: EN_LCD_OUT = EN_KBD_INPUT; IR_Data[7:0] = IR_Addr[7:0];
  //   IR_Addr[11:9] = I_O_Addr

  // Notes on the sheet:
  //   Equiv to 74HCT4017
  //   AT28C256 - 32k x 8 bit EEPROM x4
  //   This odd block is just to make sure the initial state on reset will always be Fetch-1 High and CLK-B Low
  //   contents of rom_1 (hex, n*v repeats v):
  //   0 c00000 600400 5e0000 4f0000 4000 6000 4200 6200 100 181800 91800 4040 4240 0 0 1400000 880 14*0
  //   408825 408818 408802 40882e 40883a 40881a 408806 408826 408800 40883d 408801 408819 408831 2400831
  //   JACA-2 - 8-bit Homebrew CPU
  //   v. 0.19.2
  //   https://hackaday.io/project/24511-jaca-1-homebrew-cpu
  //   Most significant byte
  //   PC: 74LS161 - 4 bit counter x3
  //   74LS154 - 4-16 line decoder
  //   SRAM 62256 32k x 8 bit
  //   RAM
  //   REG_IN
  //   74ALS874 - 8 bit register x8
  //   74ALS874 - 8 bit register x3
  //   Least significant byte
  //   74LS154 - 4-16 line decoder
  //   This DMX should be traded by a Decoder
  //   1602 - 16 col x 2 lines LCD display
endmodule

module Instruction_Decoder (
  input  A5,
  input  A4,
  input  A3,
  input  A2,
  input  A1,
  input  A0,
  output IR_DATA_to_REG_IN,
  output EN_REG_CLK,
  output OUT_REG_to_REG_IN,
  output IR_ADDR_to_MEM_ADDR,
  output EN_MEM,
  output MEM_READ,
  output MEM_DATA_to_REG_IN,
  output RR3_to_MEM_ADDR,
  output ALU_OUT_to_REG_IN,
  output IR_ADDR_to_PC,
  output Z_FLAG_to_IR_ADDR_to_PC,
  output R1_to_MEM_DATA
);

  wire and_1_out, and_2_out, and_4_out, and_5_out, and_6_out, and_7_out, and_9_out, and_10_out, and_11_out,
       and_12_out, and_13_out, and_14_out, and_15_out, and_16_out, and_17_out, and_18_out, and_19_out,
       and_20_out, and_21_out, and_22_out, and_23_out, and_24_out, and_25_out, and_26_out, not_1_out,
       not_2_out, not_3_out, not_4_out, not_5_out, not_6_out, not_7_out, not_8_out, not_9_out, not_10_out,
       not_11_out, not_12_out, not_13_out, not_14_out, not_15_out, not_16_out, not_17_out, not_18_out,
       not_19_out, not_20_out, not_21_out, not_22_out, not_23_out, not_24_out, not_25_out, not_26_out,
       not_27_out, not_28_out, not_29_out, not_30_out, not_31_out, not_32_out, not_33_out, not_34_out,
       not_35_out, not_36_out, not_37_out, not_38_out, not_39_out;

  not not_1 (not_1_out, A3);
  not not_2 (not_2_out, A2);
  not not_3 (not_3_out, A1);
  not not_4 (not_4_out, A3);
  not not_5 (not_5_out, A2);
  not not_6 (not_6_out, A0);
  not not_7 (not_7_out, A3);
  not not_8 (not_8_out, A2);
  not not_9 (not_9_out, A1);
  not not_10 (not_10_out, A3);
  not not_11 (not_11_out, A2);
  not not_12 (not_12_out, A0);
  not not_13 (not_13_out, A3);
  not not_14 (not_14_out, A2);
  not not_15 (not_15_out, A3);
  not not_16 (not_16_out, A2);
  not not_17 (not_17_out, A3);
  not not_18 (not_18_out, A1);
  not not_19 (not_19_out, A0);
  not not_20 (not_20_out, A3);
  not not_21 (not_21_out, A3);
  not not_22 (not_22_out, A3);
  not not_23 (not_23_out, A2);
  not not_24 (not_24_out, A3);
  not not_25 (not_25_out, A1);
  not not_26 (not_26_out, A0);
  not not_27 (not_27_out, A3);
  not not_28 (not_28_out, A1);
  not not_29 (not_29_out, A0);
  not not_30 (not_30_out, A3);
  not not_31 (not_31_out, A3);
  not not_32 (not_32_out, A2);
  not not_33 (not_33_out, A1);
  not not_34 (not_34_out, A2);
  not not_35 (not_35_out, A0);
  not not_36 (not_36_out, A1);
  not not_37 (not_37_out, A0);
  not not_38 (not_38_out, A1);
  not not_39 (not_39_out, A0);
  and and_1 (and_1_out, A3, A2, A0);
  and and_2 (and_2_out, A3, A2, A1);
  and and_3 (IR_DATA_to_REG_IN, not_1_out, not_2_out, not_3_out, A0);
  and and_4 (and_4_out, not_4_out, A0);
  and and_5 (and_5_out, not_5_out, A1, not_6_out);
  and and_6 (and_6_out, not_7_out, A2);
  and and_7 (and_7_out, A3, not_8_out, not_9_out);
  and and_8 (OUT_REG_to_REG_IN, not_10_out, not_11_out, A1, not_12_out);
  and and_9 (and_9_out, not_13_out, not_14_out, A1, A0);
  and and_10 (and_10_out, A3, A2, A0);
  and and_11 (and_11_out, not_15_out, not_16_out, A1, A0);
  and and_12 (and_12_out, not_17_out, A2, not_18_out, not_19_out);
  and and_13 (and_13_out, A3, A2, A0);
  and and_14 (and_14_out, A3, A2, A1);
  and and_15 (and_15_out, not_20_out, A1);
  and and_16 (and_16_out, not_21_out, A2);
  and and_17 (and_17_out, not_22_out, not_23_out, A1, A0);
  and and_18 (and_18_out, not_24_out, A2, not_25_out, not_26_out);
  and and_19 (and_19_out, not_27_out, A2, not_28_out, not_29_out);
  and and_20 (and_20_out, A3, A2, A1);
  and and_21 (and_21_out, not_30_out, A2, A0);
  and and_22 (and_22_out, not_31_out, A2, A1);
  and and_23 (and_23_out, A3, not_32_out, not_33_out);
  and and_24 (and_24_out, A3, not_34_out, not_35_out);
  and and_25 (and_25_out, A3, A1, A0);
  and and_26 (and_26_out, A3, A2, not_36_out, not_37_out);
  and and_27 (Z_FLAG_to_IR_ADDR_to_PC, A3, A2, not_38_out, not_39_out);
  or or_1 (R1_to_MEM_DATA, and_1_out, and_2_out);
  or or_2 (EN_REG_CLK, and_4_out, and_5_out, and_6_out, and_7_out);
  or or_3 (IR_ADDR_to_MEM_ADDR, and_9_out, and_10_out);
  or or_4 (EN_MEM, and_11_out, and_12_out, and_13_out, and_14_out);
  or or_5 (MEM_READ, and_15_out, and_16_out);
  or or_6 (MEM_DATA_to_REG_IN, and_17_out, and_18_out);
  or or_7 (RR3_to_MEM_ADDR, and_19_out, and_20_out);
  or or_8 (ALU_OUT_to_REG_IN, and_21_out, and_22_out, and_23_out, and_24_out);
  or or_9 (IR_ADDR_to_PC, and_25_out, and_26_out);
endmodule

module Instruction_Decoder__cont (
  input  A5,
  input  A4,
  input  A3,
  input  A2,
  input  A1,
  input  A0,
  output ALU_F3,
  output ALU_F2,
  output ALU_F1,
  output ALU_F0,
  output ALU_M,
  output ALU_C
);

  wire and_1_out, and_2_out, and_3_out, and_4_out, and_5_out, not_2_out, not_3_out, not_4_out, not_5_out,
       not_6_out, not_7_out, not_8_out, not_9_out, not_10_out;

  not not_1 (ALU_F3, A1);
  not not_2 (not_2_out, A2);
  not not_3 (not_3_out, A0);
  not not_4 (not_4_out, A2);
  not not_5 (not_5_out, A0);
  not not_6 (not_6_out, A3);
  not not_7 (not_7_out, A1);
  not not_8 (not_8_out, A1);
  not not_9 (not_9_out, A0);
  not not_10 (not_10_out, A2);
  and and_1 (and_1_out, A1, A0);
  not not_11 (ALU_C, A1);
  and and_2 (and_2_out, not_2_out, A0);
  and and_3 (and_3_out, A1, not_3_out);
  or or_1 (ALU_F1, not_4_out, not_5_out);
  and and_4 (and_4_out, not_6_out, not_7_out);
  and and_5 (and_5_out, not_8_out, not_9_out);
  or or_2 (ALU_M, not_10_out, and_1_out);
  or or_3 (ALU_F2, and_2_out, and_3_out);
  or or_4 (ALU_F0, and_4_out, and_5_out);
endmodule

module TEST (
  input  IR_ADDR_TO_PC,
  input  EXECUTE,
  input  Z_FLAG,
  input  Z_FLAG_TO_IR,
  output OUT
);

  wire not_1_out, or_1_out;

  or or_1 (or_1_out, Z_FLAG, not_1_out);
  not not_1 (not_1_out, Z_FLAG_TO_IR);
  and and_1 (OUT, IR_ADDR_TO_PC, EXECUTE, or_1_out);
endmodule

module test (
  input  Z,
  input  ZZ,
  input  C,
  input  CC,
  output O
);

  wire and_1_out, and_2_out, and_3_out, not_1_out, not_2_out, not_3_out, not_4_out;

  not not_1 (not_1_out, ZZ);
  and and_1 (and_1_out, not_1_out, not_2_out);
  not not_2 (not_2_out, CC);
  not not_3 (not_3_out, ZZ);
  and and_2 (and_2_out, not_3_out, C);
  and and_3 (and_3_out, Z, not_4_out);
  not not_4 (not_4_out, CC);
  or or_1 (O, and_1_out, and_2_out, and_3_out);
endmodule
