// Logisim project Display and keyboard tests.circ as structural Verilog: 1 circuit, main circuit main
module main (
  input  [6:0] in_1,
  input  [6:0] in_2,
  input  [6:0] in_3,
  input  [6:0] in_4,
  input  [6:0] in_5
);

  wire clock_1_out, CLR_2_out, CLR_out;
  wire [6:0] keyboard_1_data;

  Keyboard keyboard_1 (.clk(clock_1_out), .re(1'b1), .clr(CLR_out), .data(keyboard_1_data));  // open: avail
  Clock clock_1 (.out(clock_1_out));
  _7_Segment_Display u_7_segment_display_1 ();  // open: g, f, a, b, e, d, c, dp
  Hex_Digit_Display hex_digit_display_1 ();  // open: value, dp
  Button CLR (.out(CLR_out));
  TTY tty_1 (.data(keyboard_1_data), .clk(clock_1_out), .we(1'b1), .clr(CLR_2_out));
  Button CLR_2 (.out(CLR_2_out));
  DotMatrix dotmatrix_1 (.col0(in_1), .col1(in_2), .col2(in_3), .col3(in_4), .col4(in_5));
endmodule
