// Logisim project test 74181.circ as structural Verilog: 1 circuit, main circuit main
module main (
  input  [3:0] S,
  input  [3:0] A,
  input  [3:0] B,
  input  M,
  input  Cn,
  input  [3:0] S_2,
  input  [3:0] A_2,
  input  [3:0] B_2,
  input  M_2,
  input  Cn_2,
  input  [3:0] S_3,
  input  [3:0] A_3,
  input  [3:0] B_3,
  input  M_3,
  input  Cn_3,
  output G,
  output Cn_4,
  output P,
  output A_B,
  output [3:0] F,
  output G_2,
  output Cn_4_2,
  output P_2,
  output A_B_2,
  output [3:0] F_2,
  output G_3,
  output Cn_4_3,
  output P_3,
  output A_B_3,
  output [3:0] F_3
);

  wire _74181v1_cn_4, _74181v2_p12, _74181v3_cn_4, not_1_out, not_2_out, not_3_out;

  not not_1 (not_1_out, Cn);
  not not_2 (not_2_out, Cn_2);
  not not_3 (not_3_out, Cn_3);
  _74181 _74181v1 (
    .S3(S[3]), .S2(S[2]), .S1(S[1]), .S0(S[0]), .B3(B[3]), .A3(A[3]), .B2(B[2]), .A2(A[2]), .B1(B[1]),
    .A1(A[1]), .B0(B[0]), .A0(A[0]), .M(M), .Cn(not_1_out), .G(G), .Cn_4(_74181v1_cn_4), .P(P), .F3(F[3]),
    .F2(F[2]), .A_B(A_B), .F1(F[1]), .F0(F[0]));
  // _74181 _74181v2: pin names not known; wires that end beside it: B_2[3], A_2[3], B_2[2], A_2[2], B_2[1], A_2[1], B_2[0], A_2[0], M_2, not_2_out, G_2, _74181v2_p12, P_2, F_2[3], F_2[2], A_B_2, F_2[1], F_2[0]
  _74181 _74181v3 (
    .S3(S_3[3]), .S2(S_3[2]), .S1(S_3[1]), .S0(S_3[0]), .B3(B_3[3]), .A3(A_3[3]), .B2(B_3[2]), .A2(A_3[2]),
    .B1(B_3[1]), .A1(A_3[1]), .B0(B_3[0]), .A0(A_3[0]), .M(M_3), .Cn(not_3_out), .G(G_3),
    .Cn_4(_74181v3_cn_4), .P(P_3), .F3(F_3[3]), .F2(F_3[2]), .A_B(A_B_3), .F1(F_3[1]), .F0(F_3[0]));
  not not_4 (Cn_4, _74181v1_cn_4);
  not not_5 (Cn_4_2, _74181v2_p12);
  not not_6 (Cn_4_3, _74181v3_cn_4);
endmodule
