// Logisim project test 8 bit 74181.circ as structural Verilog: 1 circuit, main circuit main
module main (
  input  [7:0] in_1,
  input  [7:0] in_2,
  input  [3:0] S,
  input  [7:0] A,
  input  M,
  input  Cn,
  input  [7:0] B,
  output G,
  output A__B,
  output Cn_4,
  output P,
  output A_B,
  output A_B_2,
  output A_B_3,
  output A__B_2,
  output [7:0] F,
  output G_2,
  output Cn_4_2,
  output P_2,
  output A_B_4
);

  wire n74181_1_cn_4, n74181_2_cn_4;
  wire [7:0] adder_1_out;

  _74181 u_74181_1 (
    .S3(S[3]), .S2(S[2]), .S1(S[1]), .S0(S[0]), .B3(B[3]), .A3(A[3]), .B2(B[2]), .A2(A[2]), .B1(B[1]),
    .A1(A[1]), .B0(B[0]), .A0(A[0]), .M(M), .Cn(Cn), .G(G), .Cn_4(n74181_1_cn_4), .P(P), .F3(F[3]),
    .F2(F[2]), .A_B(A_B_2), .F1(F[1]), .F0(F[0]));
  _74181 u_74181_2 (
    .S3(S[3]), .S2(S[2]), .S1(S[1]), .S0(S[0]), .B3(B[7]), .A3(A[7]), .B2(B[6]), .A2(A[6]), .B1(B[5]),
    .A1(A[5]), .B0(B[4]), .A0(A[4]), .M(M), .Cn(n74181_1_cn_4), .G(G_2), .Cn_4(n74181_2_cn_4), .P(P_2),
    .F3(F[7]), .F2(F[6]), .A_B(A_B_4), .F1(F[5]), .F0(F[4]));
  not not_1 (Cn_4, n74181_1_cn_4);
  not not_2 (Cn_4_2, n74181_2_cn_4);
  Adder adder_1 (.a(in_1), .b(in_2), .out(adder_1_out));  // open: cin, cout
  // Probe on adder_1_out
  and and_1 (A__B, n74181_1_cn_4, Cn);
  and and_2 (A_B, n74181_1_cn_4, ~Cn);  // AND_Gate
  and and_3 (A_B_3, ~n74181_1_cn_4, Cn);  // AND_Gate
  and and_4 (A__B_2, ~n74181_1_cn_4, ~Cn);  // AND_Gate

  // Notes on the sheet:
  //   LSB
  //   MSB
endmodule
