// Logisim project tetris.circ as structural Verilog: 4 circuits, main circuit main
module main (
);

  wire and_1_out, and_2_out, and_3_out, and_4_out, button_2_out, button_out, clock_1_out, comparator_2_eq,
       d_ff_1_qn, GKEY_out, HALT_out, JMP_out, JMPZ_out, LOAD_out, not_1_out, not_2_out, not_3_out,
       not_4_out, not_5_out, not_6_out, not_7_out, not_8_out, not_9_out, not_10_out, not_11_out, not_12_out,
       not_13_out, not_15_out, not_16_out, not_17_out, not_18_out, not_19_out, not_20_out, not_21_out,
       not_22_out, not_23_out, not_24_out, not_25_out, not_26_out, not_27_out, or_1_out, or_4_out, or_5_out,
       PNTi_out, R_out, RNDR_out, SPNT_out, ST_out, STAV_q, STAV_qn;
  wire [0:0] disp_1_current;
  wire [1:0] comparator_1_gt, or_2_out, register_1_q;
  wire [2:0] multiplexer_6_out, regs_1_reg1_2;
  wire [3:0] multiplexer_4_out_3, multiplexer_4_out_4, multiplexer_7_out, regs_1_reg2_2;
  wire [7:0] disp_1_out_6, disp_1_out_7, disp_1_out_8, disp_1_out_9, disp_1_out_10, disp_1_out_11,
       disp_1_out_12, disp_1_out_13, disp_1_out_14, disp_1_out_15, disp_1_out_16, disp_1_out_17;
  wire [10:0] adder_1_out, adder_2_out, divider_1_rem, multiplexer_1_out, multiplexer_2_out,
       multiplexer_3_out, multiplexer_5_out, not_14_out, ram_1_data, register_2_q, regs_1_nreg_2,
       rom_1_data_2;
  wire [10:3] regs_1_reg1;
  wire [10:4] multiplexer_4_out, regs_1_reg2;
  wire [22:11] multiplexer_4_out_2;
  wire [26:0] register_3_q;
  wire [26:11] rom_1_data;
  wire [31:0] counter_1_q;

  disp disp_1 (
    .hodn(regs_1_nreg_2[0]), .X(multiplexer_6_out), .clock(SPNT_out), .Y(multiplexer_7_out), .rndr(RNDR_out),
    .out_6(disp_1_out_6), .out_7(disp_1_out_7), .out_8(disp_1_out_8), .out_9(disp_1_out_9),
    .out_10(disp_1_out_10), .out_11(disp_1_out_11), .out_12(disp_1_out_12), .out_13(disp_1_out_13),
    .out_14(disp_1_out_14), .out_15(disp_1_out_15), .out_16(disp_1_out_16), .out_17(disp_1_out_17),
    .current(disp_1_current[0]));
  DotMatrix #(.inputtype("row"), .matrixcols(8), .matrixrows(12)) dotmatrix_1 (
    .row0(disp_1_out_6), .row1(disp_1_out_7), .row2(disp_1_out_8), .row3(disp_1_out_9), .row4(disp_1_out_10),
    .row5(disp_1_out_11), .row6(disp_1_out_12), .row7(disp_1_out_13), .row8(disp_1_out_14),
    .row9(disp_1_out_15), .row10(disp_1_out_16), .row11(disp_1_out_17));
  Button button (.out(button_out));
  Button R (.out(R_out));
  Button button_2 (.out(button_2_out));
  not not_1 (not_1_out, button_out);
  not not_2 (not_2_out, button_2_out);
  or or_1 (or_1_out, button_out, R_out, button_2_out);
  not not_3 (not_3_out, not_1_out);
  not not_4 (not_4_out, not_2_out);
  not not_5 (not_5_out, not_3_out);
  not not_6 (not_6_out, not_4_out);
  not not_7 (not_7_out, not_5_out);
  not not_8 (not_8_out, not_6_out);
  or or_2 (or_2_out[0], not_7_out, not_12_out);
  or or_3 (or_2_out[1], not_12_out, not_8_out);
  Multiplexer #(.width(11)) multiplexer_1 (
    .in0(adder_2_out), .in1({regs_1_reg1, regs_1_reg1_2}), .out(multiplexer_1_out), .sel(or_5_out));  // open: en
  Clock clock_1 (.out(clock_1_out));
  D_Flip_Flop d_ff_1 (.Qn(d_ff_1_qn), .preset(and_1_out));  // open: clk, D, Q, en, reset
  not not_9 (not_9_out, R_out);
  and and_1 (and_1_out, and_3_out, STAV_qn, HALT_out);
  not not_10 (not_10_out, not_9_out);
  not not_11 (not_11_out, not_10_out);
  Register #(.width(2), .trigger("falling")) register_1 (
    .D(or_2_out), .Q(register_1_q), .clk(or_4_out));  // open: en, clr
  or or_4 (or_4_out, or_1_out, GKEY_out);
  not not_12 (not_12_out, not_11_out);
  Register #(.width(11), .trigger("falling")) register_2 (
    .D(multiplexer_1_out), .Q(register_2_q), .clk(and_2_out));  // open: en, clr
  and and_2 (and_2_out, and_3_out, not_13_out);
  not not_13 (not_13_out, LOAD_out);
  and and_3 (and_3_out, clock_1_out, d_ff_1_qn);
  Adder #(.width(11)) adder_1 (
    .a({regs_1_reg1, regs_1_reg1_2}), .b({regs_1_reg2, regs_1_reg2_2}), .out(adder_1_out));  // open: cin, cout
  Comparator #(.width(11)) comparator_1 (
    .a({regs_1_reg1, regs_1_reg1_2}), .b({regs_1_reg2, regs_1_reg2_2}), .gt(comparator_1_gt[0]),
    .lt(comparator_1_gt[1]));  // open: eq
  Adder #(.width(11)) adder_2 (.a(11'h1), .b(register_2_q), .out(adder_2_out));  // open: cin, cout
  Counter #(.width(32), .max('hffffffff)) counter_1 (
    .Q(counter_1_q), .clk(and_3_out));  // open: load, D, count, carry, clr
  Multiplexer #(.width(11)) multiplexer_2 (
    .in0(register_2_q), .in1({multiplexer_4_out, multiplexer_4_out_4}), .out(multiplexer_2_out), .sel(STAV_q));  // open: en
  D_Flip_Flop #(.trigger("falling")) STAV (
    .clk(and_3_out), .D(LOAD_out), .Q(STAV_q), .Qn(STAV_qn));  // open: preset, en, reset
  Multiplexer #(.select(2), .width(11)) multiplexer_3 (
    .in0({11{1'b0}}), .in1(11'h1), .in2({11{1'b1}}), .out(multiplexer_3_out), .sel(comparator_1_gt));  // open: in3, en
  assign not_14_out = ~{regs_1_reg1, regs_1_reg1_2};  // NOT_Gate not_14, 11 bits wide
  Divider #(.width(11)) divider_1 (
    .a({regs_1_reg1, regs_1_reg1_2}), .b({regs_1_reg2, regs_1_reg2_2}), .rem(divider_1_rem));  // open: out, upper
  and RNDR (RNDR_out, not_16_out, not_18_out, multiplexer_4_out_3[1], multiplexer_4_out_3[0], and_3_out);
  ROM #(.addrWidth(11), .dataWidth(27)) rom_1 (
    .addr(multiplexer_2_out), .data({rom_1_data, rom_1_data_2}));  // open: sel
  Register #(.width(27)) register_3 (
    .D({rom_1_data, rom_1_data_2}), .Q(register_3_q), .clk(and_4_out));  // open: en, clr
  and and_4 (and_4_out, and_3_out, STAV_qn);
  and GKEY (GKEY_out, not_16_out, multiplexer_4_out_3[2], multiplexer_4_out_3[1], multiplexer_4_out_3[0], and_3_out);
  Multiplexer #(.width(27)) multiplexer_4 (
    .in0({rom_1_data, rom_1_data_2}), .in1(register_3_q),
    .out({multiplexer_4_out_3, multiplexer_4_out_2, multiplexer_4_out, multiplexer_4_out_4}), .sel(STAV_q));  // open: en
  not not_15 (not_15_out, multiplexer_4_out_3[0]);
  not not_16 (not_16_out, multiplexer_4_out_3[3]);
  not not_17 (not_17_out, multiplexer_4_out_3[1]);
  not not_18 (not_18_out, multiplexer_4_out_3[2]);
  and HALT (HALT_out, not_16_out, not_18_out, not_17_out, not_15_out);
  not not_19 (not_19_out, multiplexer_4_out_3[3]);
  and PNTi (PNTi_out, not_19_out, multiplexer_4_out_3[2], multiplexer_4_out_3[1], multiplexer_4_out_3[0]);
  Multiplexer #(.select(4), .width(11)) multiplexer_5 (
    .in0(regs_1_nreg_2), .in1(rom_1_data_2), .in2(adder_1_out), .in3(regs_1_nreg_2), .in4(multiplexer_3_out),
    .in5({regs_1_reg1, regs_1_reg1_2}), .in6({{10{1'b0}}, disp_1_current[0]}),
    .in7({{9{1'b0}}, register_1_q}), .in8(regs_1_nreg_2), .in9(regs_1_nreg_2), .in10(regs_1_nreg_2),
    .in11(not_14_out), .in12(counter_1_q[18:8]), .in13(ram_1_data), .in14(regs_1_nreg_2),
    .in15(divider_1_rem), .out(multiplexer_5_out), .sel(multiplexer_4_out_3));  // open: en
  and LOAD (LOAD_out, not_16_out, not_18_out, not_17_out, multiplexer_4_out_3[0]);
  not not_20 (not_20_out, multiplexer_4_out_3[1]);
  not not_21 (not_21_out, multiplexer_4_out_3[0]);
  not not_22 (not_22_out, multiplexer_4_out_3[2]);
  not not_23 (not_23_out, multiplexer_4_out_3[2]);
  and SPNT (SPNT_out, multiplexer_4_out_3[3], not_23_out, and_3_out, not_20_out, not_21_out);
  not not_24 (not_24_out, multiplexer_4_out_3[1]);
  not not_25 (not_25_out, multiplexer_4_out_3[2]);
  and JMP (JMP_out, multiplexer_4_out_3[3], not_22_out, not_24_out, multiplexer_4_out_3[0]);
  and JMPZ (JMPZ_out, multiplexer_4_out_3[3], not_25_out, multiplexer_4_out_3[1], comparator_2_eq, not_26_out);
  or or_5 (or_5_out, JMP_out, JMPZ_out);
  regs regs_1 (
    .CLOCK(and_3_out), .R1(multiplexer_4_out_2[22:19]), .R2(multiplexer_4_out_2[18:15]),
    .NREG(multiplexer_4_out_2[14:11]), .NVAL(multiplexer_5_out),
    .VAL({multiplexer_4_out, multiplexer_4_out_4}), .REALCLOCK(and_3_out),
    .REG1({regs_1_reg1, regs_1_reg1_2}), .REG2({regs_1_reg2, regs_1_reg2_2}), .NREG_2(regs_1_nreg_2));
  not not_26 (not_26_out, multiplexer_4_out_3[0]);
  Comparator #(.width(11)) comparator_2 (
    .a({regs_1_reg2, regs_1_reg2_2}), .b({11{1'b0}}), .eq(comparator_2_eq));  // open: gt, lt
  not not_27 (not_27_out, multiplexer_4_out_3[0]);
  and ST (ST_out, multiplexer_4_out_3[3], multiplexer_4_out_3[2], multiplexer_4_out_3[1], not_27_out, and_3_out);
  Multiplexer #(.width(3)) multiplexer_6 (
    .in0(regs_1_reg1_2), .in1(multiplexer_4_out[6:4]), .out(multiplexer_6_out), .sel(PNTi_out));  // open: en
  Multiplexer #(.width(4)) multiplexer_7 (
    .in0(regs_1_reg2_2), .in1(multiplexer_4_out_4), .out(multiplexer_7_out), .sel(PNTi_out));  // open: en
  RAM #(.addrWidth(11), .dataWidth(11), .bus("separate")) ram_1 (
    .addr({regs_1_reg1, regs_1_reg1_2}), .din(regs_1_nreg_2), .data(ram_1_data), .clk(ST_out));  // open: str, sel, ld, clr

  // Notes on the sheet:
  //   contents of rom_1 (hex, n*v repeats v):
  //   7f78807 20f9000 2f85000 579000f 20f9001 5790050 20f9002 5790091 20f9003 57900d2 20f9004 5790113
  //   20f9005 5790154 4f80195 2f80800 7780800 2f80800 7780801 2f80801 7780802 2f80800 7780803 2f80802
  //   7780804 2f80800 7780805 2f80803 7780806 2f80800 7780807 2f80800 7780808 2f80800 7780809 2f80800
  //   778080a 2f80801 778080b 2f80800 778080c 2f80802 778080d 2f80800 778080e 2f80803 778080f 2f80800
  //   7780810 2f80800 7780811 2f80801 7780812 2f80800 7780813 2f80802 7780814 2f80800 7780815 2f80803
  //   7780816 2f80800 7780817 2f80800 7780818 2f80800 7780819 2f80800 778081a 2f80801 778081b 2f80800
  //   778081c 2f80802 778081d 2f80800 778081e 2f80803 778081f 4f806f3 2f80800 7780800 2f80800 7780801
  //   2f80800 7780802 2f80801 7780803 2f80801 7780804 2f80801 7780805 2f80802 7780806 2f80801 7780807
  //   2f80801 7780808 2f80800 7780809 2f80801 778080a 2f80801 778080b 2f80801 778080c 2f80802 778080d
  //   2f80800 778080e 2f80802 778080f 2f80800 7780810 2f80800 7780811 2f80801 7780812 2f80800 7780813
  //   2f80802 7780814 2f80800 7780815 2f80802 7780816 2f80801 7780817 2f80800 7780818 2f80800 7780819
  //   2f80801 778081a 2f80800 778081b 2f80800 778081c 2f80801 778081d 2f80800 778081e 2f80802 778081f
  //   4f806f3 2f80800 7780800 2f80801 7780801 2f80801 7780802 2f80801 7780803 2f80802 7780804 2f80801
  //   7780805 2f80802 7780806 2f80800 7780807 2f80800 7780808 2f80800 7780809 2f80801 778080a 2f80800
  //   778080b 2f80801 778080c 2f80801 778080d 2f80801 778080e 2f80802 778080f 2f80800 7780810 2f80800
  //   7780811 2f80801 7780812 2f80800 7780813 2f80802 7780814 2f80800 7780815 2f80800 7780816 2f80801
  //   7780817 2f80800 7780818 2f80800 7780819 2f80800 778081a 2f80801 778081b 2f80800 778081c 2f80802
  //   778081d 2f80801 778081e 2f80802 778081f 4f806f3 2f80800 7780800 2f80800 7780801 2f80801 7780802
  //   2f80800 7780803 2f80800 7780804 2f80801 7780805 2f80801 7780806 2f80801 7780807 2f80800 7780808
  //   2f80800 7780809 2f80801 778080a 2f80800 778080b 2f80800 778080c 2f80801 778080d 2f80801 778080e
  //   2f80801 778080f 2f80800 7780810 2f80800 7780811 2f80801 7780812 2f80800 7780813 2f80800 7780814
  //   2f80801 7780815 2f80801 7780816 2f80801 7780817 2f80800 7780818 2f80800 7780819 2f80801 778081a
  //   2f80800 778081b 2f80800 778081c 2f80801 778081d 2f80801 778081e 2f80801 778081f 4f806f3 2f80801
  //   7780800 2f80800 7780801 2f80802 7780802 2f80800 7780803 2f80800 7780804 2f80801 7780805 2f80801
  //   7780806 2f80801 7780807 2f80800 7780808 2f80800 7780809 2f80800 778080a 2f80801 778080b 2f80801
  //   778080c 2f80801 778080d 2f80801 778080e 2f80802 778080f 2f80801 7780810 2f80800 7780811 2f80802
  //   7780812 2f80800 7780813 2f80800 7780814 2f80801 7780815 2f80801 7780816 2f80801 7780817 2f80800
  //   7780818 2f80800 7780819 2f80800 778081a 2f80801 778081b 2f80801 778081c 2f80801 778081d 2f80801
  //   778081e 2f80802 778081f 4f806f3 2f80800 7780800 2f80801 7780801 2f80801 7780802 2f80801 7780803
  //   2f80802 7780804 2f80801 7780805 2f80801 7780806 2f80800 7780807 2f80801 7780808 2f80800 7780809
  //   2f80801 778080a 2f80801 778080b 2f80801 778080c 2f80802 778080d 2f80800 778080e 2f80801 778080f
  //   2f80800 7780810 2f80800 7780811 2f80801 7780812 2f80800 7780813 2f80802 7780814 2f80800 7780815
  //   2f80801 7780816 2f80801 7780817 2f80800 7780818 2f80800 7780819 2f80800 778081a 2f80801 778081b
  //   2f80800 778081c 2f80802 778081d 2f80801 778081e 2f80801 778081f 4f806f3 2f80800 7780800 2f80800
  //   7780801 2f80801 7780802 2f80800 7780803 2f80801 7780804 2f80801 7780805 2f80802 7780806 2f80801
  //   7780807 2f80801 7780808 2f80800 7780809 2f80801 778080a 2f80801 778080b 2f80800 778080c 2f80801
  //   778080d 2f80800 778080e 2f80802 778080f 2f80800 7780810 2f80800 7780811 2f80801 7780812 2f80800
  //   7780813 2f80801 7780814 2f80801 7780815 2f80802 7780816 2f80801 7780817 2f80801 7780818 2f80800
  //   7780819 2f80801 778081a 2f80801 778081b 2f80800 778081c 2f80801 778081d 2f80800 778081e 2f80802
  //   778081f 4f806f3 27d1800 57981eb 27d1801 5798215 27d1802 579823f 4f80269 27d1800 5798200 27d1801
  //   579822a 27d1802 5798254 4f8027e 27d1800 579865b 27d1801 57985e1 27d1802 5798567 4f804ed 6f81800
  //   6f82001 1099800 1122000 41a7801 6f81802 6f82003 1099800 1122000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
endmodule

module dispriadok (
  input  clock,
  input  hodn,
  input  [2:0] X,
  output [7:0] riadok,
  output single
);

  wire demultiplexer_1_out0, demultiplexer_1_out1, demultiplexer_1_out2, demultiplexer_1_out3,
       demultiplexer_1_out4, demultiplexer_1_out5, demultiplexer_1_out6, demultiplexer_1_out7;

  Demultiplexer #(.select(3)) demultiplexer_1 (
    .out0(demultiplexer_1_out0), .out1(demultiplexer_1_out1), .out2(demultiplexer_1_out2),
    .out3(demultiplexer_1_out3), .out4(demultiplexer_1_out4), .out5(demultiplexer_1_out5),
    .out6(demultiplexer_1_out6), .out7(demultiplexer_1_out7), .in(clock), .sel(X));  // open: en
  D_Flip_Flop d_ff_1 (.clk(demultiplexer_1_out0), .D(hodn), .Q(riadok[7]));  // open: Qn, preset, en, reset
  D_Flip_Flop d_ff_2 (.clk(demultiplexer_1_out1), .D(hodn), .Q(riadok[6]));  // open: Qn, preset, en, reset
  D_Flip_Flop d_ff_3 (.clk(demultiplexer_1_out2), .D(hodn), .Q(riadok[5]));  // open: Qn, preset, en, reset
  D_Flip_Flop d_ff_4 (.clk(demultiplexer_1_out3), .D(hodn), .Q(riadok[4]));  // open: Qn, preset, en, reset
  D_Flip_Flop d_ff_5 (.clk(demultiplexer_1_out4), .D(hodn), .Q(riadok[3]));  // open: Qn, preset, en, reset
  D_Flip_Flop d_ff_6 (.clk(demultiplexer_1_out5), .D(hodn), .Q(riadok[2]));  // open: Qn, preset, en, reset
  D_Flip_Flop d_ff_7 (.clk(demultiplexer_1_out6), .D(hodn), .Q(riadok[1]));  // open: Qn, preset, en, reset
  D_Flip_Flop d_ff_8 (.clk(demultiplexer_1_out7), .D(hodn), .Q(riadok[0]));  // open: Qn, preset, en, reset
  Multiplexer #(.select(3)) multiplexer_1 (
    .in0(riadok[7]), .in1(riadok[6]), .in2(riadok[5]), .in3(riadok[4]), .in4(riadok[3]), .in5(riadok[2]),
    .in6(riadok[1]), .in7(riadok[0]), .out(single), .sel(X));  // open: en
endmodule

module disp (
  input  hodn,
  input  [2:0] X,
  input  clock,
  input  [3:0] Y,
  input  rndr,
  output [7:0] out_6,
  output [7:0] out_7,
  output [7:0] out_8,
  output [7:0] out_9,
  output [7:0] out_10,
  output [7:0] out_11,
  output [7:0] out_12,
  output [7:0] out_13,
  output [7:0] out_14,
  output [7:0] out_15,
  output [7:0] out_16,
  output [7:0] out_17,
  output current
);

  wire demultiplexer_1_out0, demultiplexer_1_out1, demultiplexer_1_out2, demultiplexer_1_out3,
       demultiplexer_1_out4, demultiplexer_1_out5, demultiplexer_1_out6, demultiplexer_1_out7,
       demultiplexer_1_out8, demultiplexer_1_out9, demultiplexer_1_out10, demultiplexer_1_out11,
       dispriadok_1_single, dispriadok_2_single, dispriadok_3_single, dispriadok_4_single,
       dispriadok_5_single, dispriadok_6_single, dispriadok_7_single, dispriadok_8_single,
       dispriadok_9_single, dispriadok_10_single, dispriadok_11_single, dispriadok_12_single;
  wire [7:0] dispriadok_1_riadok, dispriadok_2_riadok, dispriadok_3_riadok, dispriadok_4_riadok,
       dispriadok_5_riadok, dispriadok_6_riadok, dispriadok_7_riadok, dispriadok_8_riadok,
       dispriadok_9_riadok, dispriadok_10_riadok, dispriadok_11_riadok, dispriadok_12_riadok;

  Demultiplexer #(.select(4)) demultiplexer_1 (
    .out0(demultiplexer_1_out0), .out1(demultiplexer_1_out1), .out2(demultiplexer_1_out2),
    .out3(demultiplexer_1_out3), .out4(demultiplexer_1_out4), .out5(demultiplexer_1_out5),
    .out6(demultiplexer_1_out6), .out7(demultiplexer_1_out7), .out8(demultiplexer_1_out8),
    .out9(demultiplexer_1_out9), .out10(demultiplexer_1_out10), .out11(demultiplexer_1_out11), .in(clock),
    .sel(Y));  // open: out12, out13, out14, out15, en
  dispriadok dispriadok_1 (
    .clock(demultiplexer_1_out0), .hodn(hodn), .X(X), .riadok(dispriadok_1_riadok),
    .single(dispriadok_1_single));
  Register register_1 (.D(dispriadok_1_riadok), .Q(out_6), .clk(rndr));  // open: en, clr
  dispriadok dispriadok_2 (
    .clock(demultiplexer_1_out1), .hodn(hodn), .X(X), .riadok(dispriadok_2_riadok),
    .single(dispriadok_2_single));
  Register register_2 (.D(dispriadok_2_riadok), .Q(out_7), .clk(rndr));  // open: en, clr
  dispriadok dispriadok_3 (
    .clock(demultiplexer_1_out2), .hodn(hodn), .X(X), .riadok(dispriadok_3_riadok),
    .single(dispriadok_3_single));
  Register register_3 (.D(dispriadok_3_riadok), .Q(out_8), .clk(rndr));  // open: en, clr
  dispriadok dispriadok_4 (
    .clock(demultiplexer_1_out3), .hodn(hodn), .X(X), .riadok(dispriadok_4_riadok),
    .single(dispriadok_4_single));
  Register register_4 (.D(dispriadok_4_riadok), .Q(out_9), .clk(rndr));  // open: en, clr
  dispriadok dispriadok_5 (
    .clock(demultiplexer_1_out4), .hodn(hodn), .X(X), .riadok(dispriadok_5_riadok),
    .single(dispriadok_5_single));
  Register register_5 (.D(dispriadok_5_riadok), .Q(out_10), .clk(rndr));  // open: en, clr
  dispriadok dispriadok_6 (
    .clock(demultiplexer_1_out5), .hodn(hodn), .X(X), .riadok(dispriadok_6_riadok),
    .single(dispriadok_6_single));
  Register register_6 (.D(dispriadok_6_riadok), .Q(out_11), .clk(rndr));  // open: en, clr
  dispriadok dispriadok_7 (
    .clock(demultiplexer_1_out6), .hodn(hodn), .X(X), .riadok(dispriadok_7_riadok),
    .single(dispriadok_7_single));
  Register register_7 (.D(dispriadok_7_riadok), .Q(out_12), .clk(rndr));  // open: en, clr
  dispriadok dispriadok_8 (
    .clock(demultiplexer_1_out7), .hodn(hodn), .X(X), .riadok(dispriadok_8_riadok),
    .single(dispriadok_8_single));
  Register register_8 (.D(dispriadok_8_riadok), .Q(out_13), .clk(rndr));  // open: en, clr
  dispriadok dispriadok_9 (
    .clock(demultiplexer_1_out8), .hodn(hodn), .X(X), .riadok(dispriadok_9_riadok),
    .single(dispriadok_9_single));
  Register register_9 (.D(dispriadok_9_riadok), .Q(out_14), .clk(rndr));  // open: en, clr
  dispriadok dispriadok_10 (
    .clock(demultiplexer_1_out9), .hodn(hodn), .X(X), .riadok(dispriadok_10_riadok),
    .single(dispriadok_10_single));
  Register register_10 (.D(dispriadok_10_riadok), .Q(out_15), .clk(rndr));  // open: en, clr
  dispriadok dispriadok_11 (
    .clock(demultiplexer_1_out10), .hodn(hodn), .X(X), .riadok(dispriadok_11_riadok),
    .single(dispriadok_11_single));
  Register register_11 (.D(dispriadok_11_riadok), .Q(out_16), .clk(rndr));  // open: en, clr
  dispriadok dispriadok_12 (
    .clock(demultiplexer_1_out11), .hodn(hodn), .X(X), .riadok(dispriadok_12_riadok),
    .single(dispriadok_12_single));
  Register register_12 (.D(dispriadok_12_riadok), .Q(out_17), .clk(rndr));  // open: en, clr
  Multiplexer #(.select(4)) multiplexer_1 (
    .in0(dispriadok_1_single), .in1(dispriadok_2_single), .in2(dispriadok_3_single),
    .in3(dispriadok_4_single), .in4(dispriadok_5_single), .in5(dispriadok_6_single),
    .in6(dispriadok_7_single), .in7(dispriadok_8_single), .in8(dispriadok_9_single),
    .in9(dispriadok_10_single), .in10(dispriadok_11_single), .in11(dispriadok_12_single), .in12(1'b1),
    .in13(1'b1), .in14(1'b1), .in15(1'b1), .out(current), .sel(Y));  // open: en
endmodule

// REGISTRE
module regs (
  input  CLOCK,
  input  [3:0] R1,
  input  [3:0] R2,
  input  [3:0] NREG,
  input  [10:0] NVAL,
  input  [10:0] VAL,
  input  REALCLOCK,
  output [10:0] REG1,
  output [10:0] REG2,
  output [10:0] NREG_2
);

  wire demultiplexer_1_out1, demultiplexer_1_out2, demultiplexer_1_out3, demultiplexer_1_out4,
       demultiplexer_1_out5, demultiplexer_1_out6, demultiplexer_1_out7, demultiplexer_1_out8,
       demultiplexer_1_out9, demultiplexer_1_out10, demultiplexer_1_out11, demultiplexer_1_out12,
       demultiplexer_1_out13;
  wire [10:0] random_1_out, register_1_q, register_2_q, register_3_q, register_4_q, register_5_q,
       register_6_q, register_7_q, register_8_q, register_9_q, register_10_q, register_11_q, register_12_q,
       register_13_q;

  Demultiplexer #(.select(4)) demultiplexer_1 (
    .out1(demultiplexer_1_out1), .out2(demultiplexer_1_out2), .out3(demultiplexer_1_out3),
    .out4(demultiplexer_1_out4), .out5(demultiplexer_1_out5), .out6(demultiplexer_1_out6),
    .out7(demultiplexer_1_out7), .out8(demultiplexer_1_out8), .out9(demultiplexer_1_out9),
    .out10(demultiplexer_1_out10), .out11(demultiplexer_1_out11), .out12(demultiplexer_1_out12),
    .out13(demultiplexer_1_out13), .in(CLOCK), .sel(NREG));  // open: out0, out14, out15, en
  Register #(.width(11)) register_1 (.D(NVAL), .Q(register_1_q), .clk(demultiplexer_1_out1));  // open: en, clr
  Register #(.width(11)) register_2 (.D(NVAL), .Q(register_2_q), .clk(demultiplexer_1_out2));  // open: en, clr
  Register #(.width(11)) register_3 (.D(NVAL), .Q(register_3_q), .clk(demultiplexer_1_out3));  // open: en, clr
  Register #(.width(11)) register_4 (.D(NVAL), .Q(register_4_q), .clk(demultiplexer_1_out4));  // open: en, clr
  Register #(.width(11)) register_5 (.D(NVAL), .Q(register_5_q), .clk(demultiplexer_1_out5));  // open: en, clr
  Register #(.width(11)) register_6 (.D(NVAL), .Q(register_6_q), .clk(demultiplexer_1_out6));  // open: en, clr
  Register #(.width(11)) register_7 (.D(NVAL), .Q(register_7_q), .clk(demultiplexer_1_out7));  // open: en, clr
  Register #(.width(11)) register_8 (.D(NVAL), .Q(register_8_q), .clk(demultiplexer_1_out8));  // open: en, clr
  Register #(.width(11)) register_9 (.D(NVAL), .Q(register_9_q), .clk(demultiplexer_1_out9));  // open: en, clr
  Register #(.width(11)) register_10 (.D(NVAL), .Q(register_10_q), .clk(demultiplexer_1_out10));  // open: en, clr
  Register #(.width(11)) register_11 (.D(NVAL), .Q(register_11_q), .clk(demultiplexer_1_out11));  // open: en, clr
  Register #(.width(11)) register_12 (.D(NVAL), .Q(register_12_q), .clk(demultiplexer_1_out12));  // open: en, clr
  Register #(.width(11)) register_13 (.D(NVAL), .Q(register_13_q), .clk(demultiplexer_1_out13));  // open: en, clr
  Random #(.width(11)) random_1 (.clk(REALCLOCK), .out(random_1_out));  // open: next, clr
  Multiplexer #(.select(4), .width(11)) multiplexer_1 (
    .in0({11{1'b0}}), .in1(register_1_q), .in2(register_2_q), .in3(register_3_q), .in4(register_4_q),
    .in5(register_5_q), .in6(register_6_q), .in7(register_7_q), .in8(register_8_q), .in9(register_9_q),
    .in10(register_10_q), .in11(register_11_q), .in12(register_12_q), .in13(register_13_q),
    .in14(random_1_out), .in15(VAL), .out(REG1), .sel(R1));  // open: en
  Multiplexer #(.select(4), .width(11)) multiplexer_2 (
    .in0({11{1'b0}}), .in1(register_1_q), .in2(register_2_q), .in3(register_3_q), .in4(register_4_q),
    .in5(register_5_q), .in6(register_6_q), .in7(register_7_q), .in8(register_8_q), .in9(register_9_q),
    .in10(register_10_q), .in11(register_11_q), .in12(register_12_q), .in13(register_13_q),
    .in14(random_1_out), .in15(VAL), .out(REG2), .sel(R2));  // open: en
  Multiplexer #(.select(4), .width(11)) multiplexer_3 (
    .in0({11{1'b0}}), .in1(register_1_q), .in2(register_2_q), .in3(register_3_q), .in4(register_4_q),
    .in5(register_5_q), .in6(register_6_q), .in7(register_7_q), .in8(register_8_q), .in9(register_9_q),
    .in10(register_10_q), .in11(register_11_q), .in12(register_12_q), .in13(register_13_q),
    .in14(random_1_out), .in15(VAL), .out(NREG_2), .sel(NREG));  // open: en
endmodule
